// Logisim project 2.circ as structural Verilog: 6 circuits, main circuit main
module main (
);

  wire _1colod, _2colod, _3colod, _4colod, _5colod, _6colod, _7colod, cancel_com, Clock, comparator_1_eq,
       comparator_2_eq, comparator_3_eq, comparator_4_eq, comparator_5_eq, comparator_6_eq, comparator_7_eq,
       comparator_8_eq, comparator_9_eq, comparator_10_eq, comparator_11_eq, comparator_12_eq,
       comparator_13_eq, comparator_14_eq, comparator_15_eq, comparator_16_eq, comparator_17_eq,
       comparator_18_eq, comparator_19_eq, comparator_20_eq, comparator_21_eq, comparator_22_eq,
       comparator_23_eq, comparator_24_eq, comparator_25_eq, comparator_26_eq, comparator_27_eq,
       comparator_28_eq, comparator_29_eq, comparator_30_eq, comparator_31_eq, comparator_32_eq,
       comparator_33_eq, comparator_34_eq, comparator_35_eq, comparator_36_eq, comparator_37_eq,
       comparator_38_eq, comparator_39_eq, comparator_40_eq, comparator_41_eq, comparator_42_eq,
       comparator_43_eq, comparator_44_eq, comparator_45_eq, comparator_46_eq, comparator_47_eq,
       comparator_48_eq, comparator_49_eq, comparator_50_eq, comparator_51_eq, comparator_52_eq,
       comparator_53_eq, comparator_54_eq, comparator_55_eq, comparator_56_eq, comparator_57_eq,
       comparator_58_eq, comparator_59_eq, comparator_60_eq, comparator_61_eq, comparator_62_eq,
       comparator_63_eq, comparator_64_eq, comparator_65_eq, comparator_66_eq, comparator_67_eq,
       comparator_68_eq, comparator_69_eq, comparator_70_eq, comparator_71_eq, comparator_72_eq,
       comparator_73_eq, comparator_74_eq, comparator_75_eq, comparator_76_eq, comparator_77_eq,
       controlled_buffer_2_out, controlled_buffer_12_out, d_ff_1_q, d_ff_2_q, data_ins, data_o, do_prog,
       first_usage, gen_clock, gen_done, gen_ld, generator_1_l_d, IAck, ins_p, IO_o, memory, move_done,
       new_com, not_1_out, not_2_out, not_3_out, or_1_out, or_2_out, or_3_out, or_4_out, print_cards_1_print,
       print_cards_2_print, pull_resistor_1_node, pull_resistor_2_node, pull_resistor_3_node,
       pull_resistor_4_node, read_write, reset, run_com, sent_done, to_print, undriven, vector_p,
       write_sentinels_1_clock_gen, write_sentinels_1_l_d, write_sentinels_2_clock_gen,
       write_sentinels_2_l_d, zeroing;
  wire [0:0] and_1_out;
  wire [2:0] priority_encoder_1_out;
  wire [3:0] _9a, _9b, _9c, _9d, _9e, _9f, _91, _92, _93, _94, _95, _96, _97, _98, a0, a1, a2, a4, a5, a6,
       a7, a8, a9, aa, ab, ac, ad, af, b0, b1, b2, b3, b4, b5, b6, b7, b8, b9, bb, bc, bd, be, bf, c0, c1,
       c2, c3, c4, c5, c6, c8, c9, ca, cb, cc, cd, ce, cf, d0, d1, d2, d3, d4, d6, d7, d8, d9, da, db, dc,
       dd, de, df, e0, e1, e2, e3, value;
  wire [7:0] addr, card_address, card_value, cdm_8_mark5_1_p9, cdm_8_mark5_1_p10, controlled_buffer_1_out,
       controlled_buffer_13_out, counter_1_q, current_command, data_base, gen_address, gen_data,
       generator_1_data, multiplexer_4_out, print_cards_1_adr, print_cards_2_adr, register_78_q,
       write_sentinels_1_address, write_sentinels_1_data, write_sentinels_2_address, write_sentinels_2_data;

  D_Flip_Flop d_ff_1 (.Q(d_ff_1_q), .preset(do_prog), .reset(IAck));  // open: clk, D, Qn, en
  and and_1 (and_1_out[0], addr[4], addr[5], addr[6], addr[7]);
  Multiplexer #(.width(8), .enable("false")) multiplexer_1 (
    .in0({8{1'b1}}), .in1(controlled_buffer_1_out), .out(card_address), .sel(to_print));
  assign controlled_buffer_1_out = gen_done ? write_sentinels_1_address : 8'bz;  // Controlled_Buffer controlled_buffer_1
  assign controlled_buffer_2_out = to_print ? pull_resistor_2_node : 1'bz;  // Controlled_Buffer controlled_buffer_2
  assign controlled_buffer_1_out = to_print ? print_cards_1_adr : 8'bz;  // Controlled_Buffer controlled_buffer_3
  Comparator comparator_1 (.a(card_address), .b(8'h91), .eq(comparator_1_eq));  // open: gt, lt
  Comparator comparator_2 (.a(card_address), .b(8'h92), .eq(comparator_2_eq));  // open: gt, lt
  Comparator comparator_3 (.a(card_address), .b(8'h93), .eq(comparator_3_eq));  // open: gt, lt
  Comparator comparator_4 (.a(card_address), .b(8'h94), .eq(comparator_4_eq));  // open: gt, lt
  Comparator comparator_5 (.a(card_address), .b(8'h95), .eq(comparator_5_eq));  // open: gt, lt
  Comparator comparator_6 (.a(card_address), .b(8'h96), .eq(comparator_6_eq));  // open: gt, lt
  Comparator comparator_7 (.a(card_address), .b(8'h97), .eq(comparator_7_eq));  // open: gt, lt
  Comparator comparator_8 (.a(card_address), .b(8'h98), .eq(comparator_8_eq));  // open: gt, lt
  Decoder #(.select(2), .disabled(0)) decoder_1 (
    .out0(ins_p), .out1(vector_p), .out2(data_o), .out3(IO_o), .sel({data_ins, and_1_out[0]}), .en(memory));
  assign controlled_buffer_2_out = gen_done ? write_sentinels_1_clock_gen : 1'bz;  // Controlled_Buffer controlled_buffer_4
  Pull_Resistor pull_resistor_1 (.node(pull_resistor_1_node));
  Pull_Resistor pull_resistor_2 (.node(pull_resistor_2_node));
  assign pull_resistor_2_node = to_print ? Clock : 1'bz;  // Controlled_Buffer controlled_buffer_5
  Multiplexer #(.width(4), .enable("false")) multiplexer_2 (
    .in0(card_value[3:0]), .in1(4'b1100), .out(value), .sel(card_value[7]));
  Register #(.width(4)) register_1 (.D(value), .Q(_91), .clk(comparator_1_eq));  // open: en, clr
  Register #(.width(4)) register_2 (.D(value), .Q(_92), .clk(comparator_2_eq));  // open: en, clr
  Register #(.width(4)) register_3 (.D(value), .Q(_93), .clk(comparator_3_eq));  // open: en, clr
  Register #(.width(4)) register_4 (.D(value), .Q(_94), .clk(comparator_4_eq));  // open: en, clr
  Register #(.width(4)) register_5 (.D(value), .Q(_95), .clk(comparator_5_eq));  // open: en, clr
  Register #(.width(4)) register_6 (.D(value), .Q(_96), .clk(comparator_6_eq));  // open: en, clr
  Register #(.width(4)) register_7 (.D(value), .Q(_97), .clk(comparator_7_eq));  // open: en, clr
  Register #(.width(4)) register_8 (.D(value), .Q(_98), .clk(comparator_8_eq));  // open: en, clr
  Clock clock_1 (.out(Clock));
  generator generator_1 (
    .clock(Clock), .reset(reset), .data(generator_1_data), .address(controlled_buffer_1_out),
    .clock_gen(controlled_buffer_2_out), .l_d(generator_1_l_d), .gen_done(gen_done));
  write_sentinels write_sentinels_1 (
    .data(write_sentinels_1_data), .clock(pull_resistor_1_node), .reset(reset),
    .address(write_sentinels_1_address), .clock_gen(write_sentinels_1_clock_gen),
    .l_d(write_sentinels_1_l_d), .sent_writing_done(sent_done));
  assign pull_resistor_1_node = gen_done ? Clock : 1'bz;  // Controlled_Buffer controlled_buffer_6
  print_cards print_cards_1 (
    .clock(pull_resistor_2_node), .adr(print_cards_1_adr), .print(print_cards_1_print), .move_done(or_1_out));
  or or_1 (or_1_out, move_done, reset);
  Comparator comparator_9 (.a(card_address), .b(8'h9a), .eq(comparator_9_eq));  // open: gt, lt
  Comparator comparator_10 (.a(card_address), .b(8'h9b), .eq(comparator_10_eq));  // open: gt, lt
  Comparator comparator_11 (.a(card_address), .b(8'h9c), .eq(comparator_11_eq));  // open: gt, lt
  Comparator comparator_12 (.a(card_address), .b(8'h9d), .eq(comparator_12_eq));  // open: gt, lt
  Comparator comparator_13 (.a(card_address), .b(8'h9e), .eq(comparator_13_eq));  // open: gt, lt
  Comparator comparator_14 (.a(card_address), .b(8'h9f), .eq(comparator_14_eq));  // open: gt, lt
  Comparator comparator_15 (.a(card_address), .b(8'ha0), .eq(comparator_15_eq));  // open: gt, lt
  Comparator comparator_16 (.a(card_address), .b(8'ha1), .eq(comparator_16_eq));  // open: gt, lt
  Comparator comparator_17 (.a(card_address), .b(8'ha2), .eq(comparator_17_eq));  // open: gt, lt
  // CdM_8_mark5 cdm_8_mark5_1: pin names not known; wires that end beside it: d_ff_1_q, 3'b000, IAck, Clock, data_ins, memory, read_write, addr, cdm_8_mark5_1_p9, cdm_8_mark5_1_p10
  assign cdm_8_mark5_1_p10 = read_write ? data_base : 8'bz;  // Controlled_Buffer controlled_buffer_7
  assign card_value = generator_1_data;  // Buffer buffer_1, 8 bits wide
  RAM ram_1 (
    .addr(controlled_buffer_1_out), .data(card_value), .clk(controlled_buffer_2_out), .ld(generator_1_l_d),
    .clr(reset));  // open: sel
  assign generator_1_l_d = gen_done ? write_sentinels_1_l_d : 1'bz;  // Controlled_Buffer controlled_buffer_8
  assign generator_1_l_d = to_print ? print_cards_1_print : 1'bz;  // Controlled_Buffer controlled_buffer_9
  Register #(.width(4)) register_9 (.D(value), .Q(_9a), .clk(comparator_9_eq));  // open: en, clr
  Register #(.width(4)) register_10 (.D(value), .Q(_9b), .clk(comparator_10_eq));  // open: en, clr
  Register #(.width(4)) register_11 (.D(value), .Q(_9c), .clk(comparator_11_eq));  // open: en, clr
  Register #(.width(4)) register_12 (.D(value), .Q(_9d), .clk(comparator_12_eq));  // open: en, clr
  Register #(.width(4)) register_13 (.D(value), .Q(_9e), .clk(comparator_13_eq));  // open: en, clr
  Register #(.width(4)) register_14 (.D(value), .Q(_9f), .clk(comparator_14_eq));  // open: en, clr
  Register #(.width(4)) register_15 (.D(value), .Q(a0), .clk(comparator_15_eq));  // open: en, clr
  Register #(.width(4)) register_16 (.D(value), .Q(a1), .clk(comparator_16_eq));  // open: en, clr
  Register #(.width(4)) register_17 (.D(value), .Q(a2), .clk(comparator_17_eq));  // open: en, clr
  assign data_base = not_1_out ? cdm_8_mark5_1_p9 : 8'bz;  // Controlled_Buffer controlled_buffer_10
  not not_1 (not_1_out, read_write);
  assign generator_1_data = gen_done ? write_sentinels_1_data : 8'bz;  // Controlled_Buffer controlled_buffer_11
  assign controlled_buffer_12_out = undriven ? 1'b0 : 1'bz;  // Controlled_Buffer controlled_buffer_12
  assign controlled_buffer_13_out = undriven ? current_command : 8'bz;  // Controlled_Buffer controlled_buffer_13
  Register #(.width(4)) register_18 (.D(value), .Q(a4), .clk(comparator_18_eq));  // open: en, clr
  Comparator comparator_18 (.a(card_address), .b(8'ha4), .eq(comparator_18_eq));  // open: gt, lt
  Register #(.width(4)) register_19 (.D(value), .Q(a5), .clk(comparator_19_eq));  // open: en, clr
  Comparator comparator_19 (.a(card_address), .b(8'ha5), .eq(comparator_19_eq));  // open: gt, lt
  Register #(.width(4)) register_20 (.D(value), .Q(a6), .clk(comparator_20_eq));  // open: en, clr
  Comparator comparator_20 (.a(card_address), .b(8'ha6), .eq(comparator_20_eq));  // open: gt, lt
  Register #(.width(4)) register_21 (.D(value), .Q(a7), .clk(comparator_21_eq));  // open: en, clr
  Comparator comparator_21 (.a(card_address), .b(8'ha7), .eq(comparator_21_eq));  // open: gt, lt
  Register #(.width(4)) register_22 (.D(value), .Q(a8), .clk(comparator_22_eq));  // open: en, clr
  Comparator comparator_22 (.a(card_address), .b(8'ha8), .eq(comparator_22_eq));  // open: gt, lt
  Register #(.width(4)) register_23 (.D(value), .Q(a9), .clk(comparator_23_eq));  // open: en, clr
  Comparator comparator_23 (.a(card_address), .b(8'ha9), .eq(comparator_23_eq));  // open: gt, lt
  Register #(.width(4)) register_24 (.D(value), .Q(aa), .clk(comparator_24_eq));  // open: en, clr
  Comparator comparator_24 (.a(card_address), .b(8'haa), .eq(comparator_24_eq));  // open: gt, lt
  Register #(.width(4)) register_25 (.D(value), .Q(ab), .clk(comparator_25_eq));  // open: en, clr
  Comparator comparator_25 (.a(card_address), .b(8'hab), .eq(comparator_25_eq));  // open: gt, lt
  Register #(.width(4)) register_26 (.D(value), .Q(ac), .clk(comparator_26_eq));  // open: en, clr
  Comparator comparator_26 (.a(card_address), .b(8'hac), .eq(comparator_26_eq));  // open: gt, lt
  Register #(.width(4)) register_27 (.D(value), .Q(ad), .clk(comparator_27_eq));  // open: en, clr
  Comparator comparator_27 (.a(card_address), .b(8'had), .eq(comparator_27_eq));  // open: gt, lt
  Register #(.width(4)) register_28 (.D(value), .Q(af), .clk(comparator_28_eq));  // open: en, clr
  Comparator comparator_28 (.a(card_address), .b(8'haf), .eq(comparator_28_eq));  // open: gt, lt
  Register #(.width(4)) register_29 (.D(value), .Q(b0), .clk(comparator_29_eq));  // open: en, clr
  Comparator comparator_29 (.a(card_address), .b(8'hb0), .eq(comparator_29_eq));  // open: gt, lt
  Register #(.width(4)) register_30 (.D(value), .Q(b1), .clk(comparator_30_eq));  // open: en, clr
  Comparator comparator_30 (.a(card_address), .b(8'hb1), .eq(comparator_30_eq));  // open: gt, lt
  Register #(.width(4)) register_31 (.D(value), .Q(b2), .clk(comparator_31_eq));  // open: en, clr
  Comparator comparator_31 (.a(card_address), .b(8'hb2), .eq(comparator_31_eq));  // open: gt, lt
  Register #(.width(4)) register_32 (.D(value), .Q(b3), .clk(comparator_32_eq));  // open: en, clr
  Comparator comparator_32 (.a(card_address), .b(8'hb3), .eq(comparator_32_eq));  // open: gt, lt
  Register #(.width(4)) register_33 (.D(value), .Q(b4), .clk(comparator_33_eq));  // open: en, clr
  Comparator comparator_33 (.a(card_address), .b(8'hb4), .eq(comparator_33_eq));  // open: gt, lt
  Register #(.width(4)) register_34 (.D(value), .Q(b5), .clk(comparator_34_eq));  // open: en, clr
  Comparator comparator_34 (.a(card_address), .b(8'hb5), .eq(comparator_34_eq));  // open: gt, lt
  Register #(.width(4)) register_35 (.D(value), .Q(b6), .clk(comparator_35_eq));  // open: en, clr
  Comparator comparator_35 (.a(card_address), .b(8'hb6), .eq(comparator_35_eq));  // open: gt, lt
  Register #(.width(4)) register_36 (.D(value), .Q(b7), .clk(comparator_36_eq));  // open: en, clr
  Comparator comparator_36 (.a(card_address), .b(8'hb7), .eq(comparator_36_eq));  // open: gt, lt
  Register #(.width(4)) register_37 (.D(value), .Q(b8), .clk(comparator_37_eq));  // open: en, clr
  Comparator comparator_37 (.a(card_address), .b(8'hb8), .eq(comparator_37_eq));  // open: gt, lt
  Register #(.width(4)) register_38 (.D(value), .Q(b9), .clk(comparator_38_eq));  // open: en, clr
  Comparator comparator_38 (.a(card_address), .b(8'hb9), .eq(comparator_38_eq));  // open: gt, lt
  assign card_value = gen_data;  // Buffer buffer_2, 8 bits wide
  RAM ram_2 (.addr(gen_address), .data(card_value), .clk(gen_clock), .ld(gen_ld), .clr(reset));  // open: sel
  Comparator comparator_39 (.a(card_address), .b(8'hbb), .eq(comparator_39_eq));  // open: gt, lt
  Comparator comparator_40 (.a(card_address), .b(8'hbc), .eq(comparator_40_eq));  // open: gt, lt
  Comparator comparator_41 (.a(card_address), .b(8'hbd), .eq(comparator_41_eq));  // open: gt, lt
  Comparator comparator_42 (.a(card_address), .b(8'hbe), .eq(comparator_42_eq));  // open: gt, lt
  Comparator comparator_43 (.a(card_address), .b(8'hbf), .eq(comparator_43_eq));  // open: gt, lt
  Comparator comparator_44 (.a(card_address), .b(8'hc0), .eq(comparator_44_eq));  // open: gt, lt
  Comparator comparator_45 (.a(card_address), .b(8'hc1), .eq(comparator_45_eq));  // open: gt, lt
  Comparator comparator_46 (.a(card_address), .b(8'hc2), .eq(comparator_46_eq));  // open: gt, lt
  Comparator comparator_47 (.a(card_address), .b(8'hc3), .eq(comparator_47_eq));  // open: gt, lt
  Comparator comparator_48 (.a(card_address), .b(8'hc4), .eq(comparator_48_eq));  // open: gt, lt
  Comparator comparator_49 (.a(card_address), .b(8'hc5), .eq(comparator_49_eq));  // open: gt, lt
  Comparator comparator_50 (.a(card_address), .b(8'hc6), .eq(comparator_50_eq));  // open: gt, lt
  Multiplexer #(.width(8), .enable("false")) multiplexer_3 (
    .in0({8{1'b1}}), .in1(gen_address), .out(card_address), .sel(to_print));
  Register #(.width(4)) register_39 (.D(value), .Q(bb), .clk(comparator_39_eq));  // open: en, clr
  Register #(.width(4)) register_40 (.D(value), .Q(bc), .clk(comparator_40_eq));  // open: en, clr
  Register #(.width(4)) register_41 (.D(value), .Q(bd), .clk(comparator_41_eq));  // open: en, clr
  Register #(.width(4)) register_42 (.D(value), .Q(be), .clk(comparator_42_eq));  // open: en, clr
  Register #(.width(4)) register_43 (.D(value), .Q(bf), .clk(comparator_43_eq));  // open: en, clr
  Register #(.width(4)) register_44 (.D(value), .Q(c0), .clk(comparator_44_eq));  // open: en, clr
  Register #(.width(4)) register_45 (.D(value), .Q(c1), .clk(comparator_45_eq));  // open: en, clr
  Register #(.width(4)) register_46 (.D(value), .Q(c2), .clk(comparator_46_eq));  // open: en, clr
  Register #(.width(4)) register_47 (.D(value), .Q(c3), .clk(comparator_47_eq));  // open: en, clr
  Register #(.width(4)) register_48 (.D(value), .Q(c4), .clk(comparator_48_eq));  // open: en, clr
  Register #(.width(4)) register_49 (.D(value), .Q(c5), .clk(comparator_49_eq));  // open: en, clr
  Register #(.width(4)) register_50 (.D(value), .Q(c6), .clk(comparator_50_eq));  // open: en, clr
  assign gen_clock = to_print ? pull_resistor_3_node : 1'bz;  // Controlled_Buffer controlled_buffer_14
  Comparator comparator_51 (.a(card_address), .b(8'hc8), .eq(comparator_51_eq));  // open: gt, lt
  Comparator comparator_52 (.a(card_address), .b(8'hc9), .eq(comparator_52_eq));  // open: gt, lt
  Comparator comparator_53 (.a(card_address), .b(8'hca), .eq(comparator_53_eq));  // open: gt, lt
  Comparator comparator_54 (.a(card_address), .b(8'hcb), .eq(comparator_54_eq));  // open: gt, lt
  Comparator comparator_55 (.a(card_address), .b(8'hcc), .eq(comparator_55_eq));  // open: gt, lt
  Comparator comparator_56 (.a(card_address), .b(8'hcd), .eq(comparator_56_eq));  // open: gt, lt
  Comparator comparator_57 (.a(card_address), .b(8'hce), .eq(comparator_57_eq));  // open: gt, lt
  Comparator comparator_58 (.a(card_address), .b(8'hcf), .eq(comparator_58_eq));  // open: gt, lt
  Comparator comparator_59 (.a(card_address), .b(8'hd0), .eq(comparator_59_eq));  // open: gt, lt
  Comparator comparator_60 (.a(card_address), .b(8'hd1), .eq(comparator_60_eq));  // open: gt, lt
  Comparator comparator_61 (.a(card_address), .b(8'hd2), .eq(comparator_61_eq));  // open: gt, lt
  Comparator comparator_62 (.a(card_address), .b(8'hd3), .eq(comparator_62_eq));  // open: gt, lt
  Comparator comparator_63 (.a(card_address), .b(8'hd4), .eq(comparator_63_eq));  // open: gt, lt
  assign gen_address = to_print ? print_cards_2_adr : 8'bz;  // Controlled_Buffer controlled_buffer_15
  Pull_Resistor pull_resistor_3 (.node(pull_resistor_3_node));
  assign pull_resistor_3_node = to_print ? Clock : 1'bz;  // Controlled_Buffer controlled_buffer_16
  or or_2 (or_2_out, move_done, reset);
  Register #(.width(4)) register_51 (.D(value), .Q(c8), .clk(comparator_51_eq));  // open: en, clr
  Register #(.width(4)) register_52 (.D(value), .Q(c9), .clk(comparator_52_eq));  // open: en, clr
  Register #(.width(4)) register_53 (.D(value), .Q(ca), .clk(comparator_53_eq));  // open: en, clr
  Register #(.width(4)) register_54 (.D(value), .Q(cb), .clk(comparator_54_eq));  // open: en, clr
  Register #(.width(4)) register_55 (.D(value), .Q(cc), .clk(comparator_55_eq));  // open: en, clr
  Register #(.width(4)) register_56 (.D(value), .Q(cd), .clk(comparator_56_eq));  // open: en, clr
  Register #(.width(4)) register_57 (.D(value), .Q(ce), .clk(comparator_57_eq));  // open: en, clr
  Register #(.width(4)) register_58 (.D(value), .Q(cf), .clk(comparator_58_eq));  // open: en, clr
  Register #(.width(4)) register_59 (.D(value), .Q(d0), .clk(comparator_59_eq));  // open: en, clr
  Register #(.width(4)) register_60 (.D(value), .Q(d1), .clk(comparator_60_eq));  // open: en, clr
  Register #(.width(4)) register_61 (.D(value), .Q(d2), .clk(comparator_61_eq));  // open: en, clr
  Register #(.width(4)) register_62 (.D(value), .Q(d3), .clk(comparator_62_eq));  // open: en, clr
  Register #(.width(4)) register_63 (.D(value), .Q(d4), .clk(comparator_63_eq));  // open: en, clr
  Button button_1 (.out(reset));
  Button button_2 (.out(run_com));
  Button button_3 (.out(cancel_com));
  Hex_Digit_Display hex_digit_display_1 (.value(current_command[7:4]));  // open: dp
  assign gen_ld = to_print ? print_cards_2_print : 1'bz;  // Controlled_Buffer controlled_buffer_17
  print_cards print_cards_2 (
    .clock(pull_resistor_3_node), .adr(print_cards_2_adr), .print(print_cards_2_print), .move_done(or_2_out));
  Hex_Digit_Display hex_digit_display_2 (.value(current_command[3:0]));  // open: dp
  Register #(.width(4)) register_64 (.D(value), .Q(d6), .clk(comparator_64_eq));  // open: en, clr
  Comparator comparator_64 (.a(card_address), .b(8'hd6), .eq(comparator_64_eq));  // open: gt, lt
  Register #(.width(4)) register_65 (.D(value), .Q(d7), .clk(comparator_65_eq));  // open: en, clr
  Comparator comparator_65 (.a(card_address), .b(8'hd7), .eq(comparator_65_eq));  // open: gt, lt
  Register #(.width(4)) register_66 (.D(value), .Q(d8), .clk(comparator_66_eq));  // open: en, clr
  Comparator comparator_66 (.a(card_address), .b(8'hd8), .eq(comparator_66_eq));  // open: gt, lt
  Register #(.width(4)) register_67 (.D(value), .Q(d9), .clk(comparator_67_eq));  // open: en, clr
  Comparator comparator_67 (.a(card_address), .b(8'hd9), .eq(comparator_67_eq));  // open: gt, lt
  Register #(.width(4)) register_68 (.D(value), .Q(da), .clk(comparator_68_eq));  // open: en, clr
  Comparator comparator_68 (.a(card_address), .b(8'hda), .eq(comparator_68_eq));  // open: gt, lt
  Register #(.width(4)) register_69 (.D(value), .Q(db), .clk(comparator_69_eq));  // open: en, clr
  Comparator comparator_69 (.a(card_address), .b(8'hdb), .eq(comparator_69_eq));  // open: gt, lt
  Register #(.width(4)) register_70 (.D(value), .Q(dc), .clk(comparator_70_eq));  // open: en, clr
  Comparator comparator_70 (.a(card_address), .b(8'hdc), .eq(comparator_70_eq));  // open: gt, lt
  Register #(.width(4)) register_71 (.D(value), .Q(dd), .clk(comparator_71_eq));  // open: en, clr
  Comparator comparator_71 (.a(card_address), .b(8'hdd), .eq(comparator_71_eq));  // open: gt, lt
  Register #(.width(4)) register_72 (.D(value), .Q(de), .clk(comparator_72_eq));  // open: en, clr
  Comparator comparator_72 (.a(card_address), .b(8'hde), .eq(comparator_72_eq));  // open: gt, lt
  Register #(.width(4)) register_73 (.D(value), .Q(df), .clk(comparator_73_eq));  // open: en, clr
  Comparator comparator_73 (.a(card_address), .b(8'hdf), .eq(comparator_73_eq));  // open: gt, lt
  Register #(.width(4)) register_74 (.D(value), .Q(e0), .clk(comparator_74_eq));  // open: en, clr
  Comparator comparator_74 (.a(card_address), .b(8'he0), .eq(comparator_74_eq));  // open: gt, lt
  Register #(.width(4)) register_75 (.D(value), .Q(e1), .clk(comparator_75_eq));  // open: en, clr
  Comparator comparator_75 (.a(card_address), .b(8'he1), .eq(comparator_75_eq));  // open: gt, lt
  Register #(.width(4)) register_76 (.D(value), .Q(e2), .clk(comparator_76_eq));  // open: en, clr
  Comparator comparator_76 (.a(card_address), .b(8'he2), .eq(comparator_76_eq));  // open: gt, lt
  Register #(.width(4)) register_77 (.D(value), .Q(e3), .clk(comparator_77_eq));  // open: en, clr
  Comparator comparator_77 (.a(card_address), .b(8'he3), .eq(comparator_77_eq));  // open: gt, lt
  not not_2 (not_2_out, not_2_out);
  Hex_Digit_Display hex_digit_display_3 (.value(_91));  // open: dp
  Hex_Digit_Display hex_digit_display_4 (.value(_92));  // open: dp
  Hex_Digit_Display hex_digit_display_5 (.value(_93));  // open: dp
  Hex_Digit_Display hex_digit_display_6 (.value(_94));  // open: dp
  Hex_Digit_Display hex_digit_display_7 (.value(_95));  // open: dp
  Hex_Digit_Display hex_digit_display_8 (.value(_96));  // open: dp
  Hex_Digit_Display hex_digit_display_9 (.value(_97));  // open: dp
  Hex_Digit_Display hex_digit_display_10 (.value(_98));  // open: dp
  assign gen_clock = gen_done ? write_sentinels_2_clock_gen : 1'bz;  // Controlled_Buffer controlled_buffer_18
  assign gen_address = gen_done ? write_sentinels_2_address : 8'bz;  // Controlled_Buffer controlled_buffer_19
  Pull_Resistor pull_resistor_4 (.node(pull_resistor_4_node));
  Button button_4 (.out(_1colod));
  generator generator_2 (
    .clock(Clock), .reset(reset), .data(gen_data), .address(gen_address), .clock_gen(gen_clock),
    .l_d(gen_ld), .gen_done(gen_done));
  assign gen_ld = gen_done ? write_sentinels_2_l_d : 1'bz;  // Controlled_Buffer controlled_buffer_20
  write_sentinels write_sentinels_2 (
    .data(write_sentinels_2_data), .clock(pull_resistor_4_node), .reset(reset),
    .address(write_sentinels_2_address), .clock_gen(write_sentinels_2_clock_gen),
    .l_d(write_sentinels_2_l_d), .sent_writing_done(sent_done));
  assign pull_resistor_4_node = gen_done ? Clock : 1'bz;  // Controlled_Buffer controlled_buffer_21
  Button button_5 (.out(_2colod));
  Hex_Digit_Display hex_digit_display_11 (.value(_9a));  // open: dp
  Hex_Digit_Display hex_digit_display_12 (.value(_9b));  // open: dp
  Hex_Digit_Display hex_digit_display_13 (.value(_9c));  // open: dp
  Hex_Digit_Display hex_digit_display_14 (.value(_9d));  // open: dp
  Hex_Digit_Display hex_digit_display_15 (.value(_9e));  // open: dp
  Hex_Digit_Display hex_digit_display_16 (.value(_9f));  // open: dp
  Hex_Digit_Display hex_digit_display_17 (.value(a0));  // open: dp
  Hex_Digit_Display hex_digit_display_18 (.value(a1));  // open: dp
  Hex_Digit_Display hex_digit_display_19 (.value(a2));  // open: dp
  assign gen_data = gen_done ? write_sentinels_2_data : 8'bz;  // Controlled_Buffer controlled_buffer_22
  or or_3 (or_3_out, _1colod, _2colod, _3colod, _4colod, _5colod, _6colod, _7colod);
  Priority_Encoder priority_encoder_1 (
    .in0(1'b0), .in1(_1colod), .in2(_2colod), .in3(_3colod), .in4(_4colod), .in5(_5colod), .in6(_6colod),
    .in7(_7colod), .out(priority_encoder_1_out), .gs(new_com));  // open: en_in, en_out
  or or_4 (or_4_out, first_usage, move_done);
  and and_2 (to_print, or_4_out, sent_done);
  and and_3 (do_prog, run_com, move_done);
  or or_5 (zeroing, reset, cancel_com, run_com);
  Button button_6 (.out(_3colod));
  Hex_Digit_Display hex_digit_display_20 (.value(a4));  // open: dp
  Hex_Digit_Display hex_digit_display_21 (.value(a5));  // open: dp
  Hex_Digit_Display hex_digit_display_22 (.value(a6));  // open: dp
  Hex_Digit_Display hex_digit_display_23 (.value(a7));  // open: dp
  Hex_Digit_Display hex_digit_display_24 (.value(a8));  // open: dp
  Hex_Digit_Display hex_digit_display_25 (.value(a9));  // open: dp
  Hex_Digit_Display hex_digit_display_26 (.value(aa));  // open: dp
  Hex_Digit_Display hex_digit_display_27 (.value(ab));  // open: dp
  Hex_Digit_Display hex_digit_display_28 (.value(ac));  // open: dp
  Hex_Digit_Display hex_digit_display_29 (.value(ad));  // open: dp
  Counter counter_1 (.Q(counter_1_q), .clk(d_ff_2_q), .clr(zeroing));  // open: load, D, count, carry
  D_Flip_Flop d_ff_2 (.Q(d_ff_2_q), .preset(or_3_out), .reset(not_3_out));  // open: clk, D, Qn, en
  not not_3 (not_3_out, or_3_out);
  Pull_Resistor pull_resistor_5 (.node(priority_encoder_1_out));
  Multiplexer #(.width(8), .enable("false")) multiplexer_4 (
    .in0(current_command), .in1({8{1'b0}}), .out(multiplexer_4_out), .sel(zeroing));
  Register register_78 (.D(multiplexer_4_out), .Q(register_78_q), .clk(Clock));  // open: en, clr
  Button button_7 (.out(_4colod));
  Hex_Digit_Display hex_digit_display_30 (.value(af));  // open: dp
  Hex_Digit_Display hex_digit_display_31 (.value(b0));  // open: dp
  Hex_Digit_Display hex_digit_display_32 (.value(b1));  // open: dp
  Hex_Digit_Display hex_digit_display_33 (.value(b2));  // open: dp
  Hex_Digit_Display hex_digit_display_34 (.value(b3));  // open: dp
  Hex_Digit_Display hex_digit_display_35 (.value(b4));  // open: dp
  Hex_Digit_Display hex_digit_display_36 (.value(b5));  // open: dp
  Hex_Digit_Display hex_digit_display_37 (.value(b6));  // open: dp
  Hex_Digit_Display hex_digit_display_38 (.value(b7));  // open: dp
  Hex_Digit_Display hex_digit_display_39 (.value(b8));  // open: dp
  Hex_Digit_Display hex_digit_display_40 (.value(b9));  // open: dp
  Comparator #(.mode("unsigned")) comparator_78 (.a(counter_1_q), .b({8{1'b0}}), .eq(first_usage));  // open: gt, lt
  card_replace card_replace_1 (
    .colod_number(priority_encoder_1_out), .cur_command(register_78_q), .updated_program(current_command),
    .move_done_updated(move_done));
  Hex_Digit_Display hex_digit_display_41 (.value(bb));  // open: dp
  Hex_Digit_Display hex_digit_display_42 (.value(bc));  // open: dp
  Hex_Digit_Display hex_digit_display_43 (.value(bd));  // open: dp
  Hex_Digit_Display hex_digit_display_44 (.value(be));  // open: dp
  Hex_Digit_Display hex_digit_display_45 (.value(bf));  // open: dp
  Hex_Digit_Display hex_digit_display_46 (.value(c0));  // open: dp
  Hex_Digit_Display hex_digit_display_47 (.value(c1));  // open: dp
  Hex_Digit_Display hex_digit_display_48 (.value(c2));  // open: dp
  Hex_Digit_Display hex_digit_display_49 (.value(c3));  // open: dp
  Hex_Digit_Display hex_digit_display_50 (.value(c4));  // open: dp
  Hex_Digit_Display hex_digit_display_51 (.value(c5));  // open: dp
  Hex_Digit_Display hex_digit_display_52 (.value(c6));  // open: dp
  Button button_8 (.out(_5colod));
  Button button_9 (.out(_6colod));
  Hex_Digit_Display hex_digit_display_53 (.value(c8));  // open: dp
  Hex_Digit_Display hex_digit_display_54 (.value(c9));  // open: dp
  Hex_Digit_Display hex_digit_display_55 (.value(ca));  // open: dp
  Hex_Digit_Display hex_digit_display_56 (.value(cb));  // open: dp
  Hex_Digit_Display hex_digit_display_57 (.value(cc));  // open: dp
  Hex_Digit_Display hex_digit_display_58 (.value(cd));  // open: dp
  Hex_Digit_Display hex_digit_display_59 (.value(ce));  // open: dp
  Hex_Digit_Display hex_digit_display_60 (.value(cf));  // open: dp
  Hex_Digit_Display hex_digit_display_61 (.value(d0));  // open: dp
  Hex_Digit_Display hex_digit_display_62 (.value(d1));  // open: dp
  Hex_Digit_Display hex_digit_display_63 (.value(d2));  // open: dp
  Hex_Digit_Display hex_digit_display_64 (.value(d3));  // open: dp
  Hex_Digit_Display hex_digit_display_65 (.value(d4));  // open: dp
  Button button_10 (.out(_7colod));
  Hex_Digit_Display hex_digit_display_66 (.value(d6));  // open: dp
  Hex_Digit_Display hex_digit_display_67 (.value(d7));  // open: dp
  Hex_Digit_Display hex_digit_display_68 (.value(d8));  // open: dp
  Hex_Digit_Display hex_digit_display_69 (.value(d9));  // open: dp
  Hex_Digit_Display hex_digit_display_70 (.value(da));  // open: dp
  Hex_Digit_Display hex_digit_display_71 (.value(db));  // open: dp
  Hex_Digit_Display hex_digit_display_72 (.value(dc));  // open: dp
  Hex_Digit_Display hex_digit_display_73 (.value(dd));  // open: dp
  Hex_Digit_Display hex_digit_display_74 (.value(de));  // open: dp
  Hex_Digit_Display hex_digit_display_75 (.value(df));  // open: dp
  Hex_Digit_Display hex_digit_display_76 (.value(e0));  // open: dp
  Hex_Digit_Display hex_digit_display_77 (.value(e1));  // open: dp
  Hex_Digit_Display hex_digit_display_78 (.value(e2));  // open: dp
  Hex_Digit_Display hex_digit_display_79 (.value(e3));  // open: dp

  // Other names for the same wires on the sheet: ram_data[7:0] = card_value; print_address[7:0] = gen_address;
  //   ram_address[7:0] = gen_address; sent_address[7:0] = gen_address; print_clock = gen_clock; ram_clock = gen_clock;
  //   sent_clock = gen_clock; sent_data[7:0] = gen_data; print_ld = gen_ld; ram_ld = gen_ld; sent_ld = gen_ld

  // Notes on the sheet:
  //   Value reading
  //   Card printer
  //   Updating indicators
  //   Reset game
  //   Run command
  //   Cancel command
  //   Current command
  //   from
  //   to
  //   C - closed card
  //   Card replacer
  //   0 - empty cell
endmodule

module configuration (
  input  [31:0] colods,
  input  clock,
  output [31:0] final_colod,
  output [3:0] card
);

  wire _1, _2, _3, _4, _5, _6, _7, _8, _9, _10, _11, _12, _13, _14, _15, _16, _17, _18, _19, _20, _21, _22,
       _23, _24, _25, _26, _27, _28, _29, _30, _31, _32, bitfinder_1_found, bitfinder_2_found,
       bitfinder_3_found, bitfinder_4_found, bitfinder_5_found, bitfinder_6_found, bitfinder_7_found,
       bitfinder_8_found, bitfinder_9_found, bitfinder_10_found, bitfinder_11_found, bitfinder_12_found,
       bitfinder_13_found, bitfinder_14_found, bitfinder_15_found, bitfinder_16_found, bitfinder_17_found,
       bitfinder_18_found, bitfinder_19_found, bitfinder_20_found, bitfinder_21_found, bitfinder_22_found,
       bitfinder_23_found, bitfinder_24_found, bitfinder_25_found, bitfinder_26_found, bitfinder_27_found,
       bitfinder_28_found, bitfinder_29_found, bitfinder_30_found, bitfinder_31_found, bitfinder_32_found;
  wire [3:0] pull_resistor_33_node, pull_resistor_34_node, pull_resistor_35_node, pull_resistor_36_node,
       pull_resistor_37_node, pull_resistor_38_node, pull_resistor_39_node, pull_resistor_40_node,
       pull_resistor_41_node, pull_resistor_42_node, pull_resistor_43_node, pull_resistor_44_node,
       pull_resistor_45_node, pull_resistor_46_node, pull_resistor_47_node, pull_resistor_48_node,
       pull_resistor_49_node, pull_resistor_50_node, pull_resistor_51_node, pull_resistor_52_node,
       pull_resistor_53_node, pull_resistor_54_node, pull_resistor_55_node, pull_resistor_56_node,
       pull_resistor_57_node, pull_resistor_58_node, pull_resistor_59_node, pull_resistor_60_node,
       pull_resistor_61_node, pull_resistor_62_node, pull_resistor_63_node, pull_resistor_64_node;
  wire [4:0] random_1_out;
  wire [31:0] n1, n2, n3, n4, n5, n6, n7, n8, n9, n10, n11, n12, n13, n14, n15, n16, n17, n18, n19, n20, n21,
       n22, n23, n24, n25, n26, n27, n28, n29, n30, n31, n32, nor_1_out, pull_resistor_1_node,
       pull_resistor_2_node, pull_resistor_3_node, pull_resistor_4_node, pull_resistor_5_node,
       pull_resistor_6_node, pull_resistor_7_node, pull_resistor_8_node, pull_resistor_9_node,
       pull_resistor_10_node, pull_resistor_11_node, pull_resistor_12_node, pull_resistor_13_node,
       pull_resistor_14_node, pull_resistor_15_node, pull_resistor_16_node, pull_resistor_17_node,
       pull_resistor_18_node, pull_resistor_19_node, pull_resistor_20_node, pull_resistor_21_node,
       pull_resistor_22_node, pull_resistor_23_node, pull_resistor_24_node, pull_resistor_25_node,
       pull_resistor_26_node, pull_resistor_27_node, pull_resistor_28_node, pull_resistor_29_node,
       pull_resistor_30_node, pull_resistor_31_node, pull_resistor_32_node;

  Decoder #(.select(5), .enable("false")) decoder_1 (
    .out0(_1), .out1(_2), .out2(_3), .out3(_4), .out4(_5), .out5(_6), .out6(_7), .out7(_8), .out8(_9),
    .out9(_10), .out10(_11), .out11(_12), .out12(_13), .out13(_14), .out14(_15), .out15(_16), .out16(_17),
    .out17(_18), .out18(_19), .out19(_20), .out20(_21), .out21(_22), .out22(_23), .out23(_24), .out24(_25),
    .out25(_26), .out26(_27), .out27(_28), .out28(_29), .out29(_30), .out30(_31), .out31(_32),
    .sel(random_1_out));
  Random #(.width(5)) random_1 (.clk(clock), .out(random_1_out));  // open: next, clr
  assign nor_1_out = ~(n1 | n2 | n3 | n4 | n5 | n6 | n7 | n8 | n9 | n10 | n11 | n12 | n13 | n14 | n15 | n16 | n17 | n18 | n19 | n20 | n21 | n22 | n23 | n24 | n25 | n26 | n27 | n28 | n29 | n30 | n31 | n32);  // NOR_Gate nor_1, 32 bits wide
  assign final_colod = nor_1_out & colods;  // AND_Gate and_1, 32 bits wide
  Pull_Resistor pull_resistor_1 (.node(pull_resistor_1_node));
  Pull_Resistor pull_resistor_2 (.node(pull_resistor_2_node));
  Pull_Resistor pull_resistor_3 (.node(pull_resistor_3_node));
  Pull_Resistor pull_resistor_4 (.node(pull_resistor_4_node));
  Pull_Resistor pull_resistor_5 (.node(pull_resistor_5_node));
  Pull_Resistor pull_resistor_6 (.node(pull_resistor_6_node));
  Pull_Resistor pull_resistor_7 (.node(pull_resistor_7_node));
  Pull_Resistor pull_resistor_8 (.node(pull_resistor_8_node));
  Pull_Resistor pull_resistor_9 (.node(pull_resistor_9_node));
  Pull_Resistor pull_resistor_10 (.node(pull_resistor_10_node));
  Pull_Resistor pull_resistor_11 (.node(pull_resistor_11_node));
  Pull_Resistor pull_resistor_12 (.node(pull_resistor_12_node));
  Pull_Resistor pull_resistor_13 (.node(pull_resistor_13_node));
  Pull_Resistor pull_resistor_14 (.node(pull_resistor_14_node));
  Pull_Resistor pull_resistor_15 (.node(pull_resistor_15_node));
  Pull_Resistor pull_resistor_16 (.node(pull_resistor_16_node));
  Pull_Resistor pull_resistor_17 (.node(pull_resistor_17_node));
  Pull_Resistor pull_resistor_18 (.node(pull_resistor_18_node));
  Pull_Resistor pull_resistor_19 (.node(pull_resistor_19_node));
  Pull_Resistor pull_resistor_20 (.node(pull_resistor_20_node));
  Pull_Resistor pull_resistor_21 (.node(pull_resistor_21_node));
  Pull_Resistor pull_resistor_22 (.node(pull_resistor_22_node));
  Pull_Resistor pull_resistor_23 (.node(pull_resistor_23_node));
  Pull_Resistor pull_resistor_24 (.node(pull_resistor_24_node));
  Pull_Resistor pull_resistor_25 (.node(pull_resistor_25_node));
  Pull_Resistor pull_resistor_26 (.node(pull_resistor_26_node));
  Pull_Resistor pull_resistor_27 (.node(pull_resistor_27_node));
  Pull_Resistor pull_resistor_28 (.node(pull_resistor_28_node));
  Pull_Resistor pull_resistor_29 (.node(pull_resistor_29_node));
  Pull_Resistor pull_resistor_30 (.node(pull_resistor_30_node));
  Pull_Resistor pull_resistor_31 (.node(pull_resistor_31_node));
  Pull_Resistor pull_resistor_32 (.node(pull_resistor_32_node));
  assign pull_resistor_1_node = _1 ? 32'h1 : 32'bz;  // Controlled_Buffer controlled_buffer_1
  assign pull_resistor_2_node = _2 ? 32'h2 : 32'bz;  // Controlled_Buffer controlled_buffer_2
  assign pull_resistor_3_node = _3 ? 32'h4 : 32'bz;  // Controlled_Buffer controlled_buffer_3
  assign pull_resistor_4_node = _4 ? 32'h8 : 32'bz;  // Controlled_Buffer controlled_buffer_4
  assign pull_resistor_5_node = _5 ? 32'h10 : 32'bz;  // Controlled_Buffer controlled_buffer_5
  assign pull_resistor_6_node = _6 ? 32'h20 : 32'bz;  // Controlled_Buffer controlled_buffer_6
  assign pull_resistor_7_node = _7 ? 32'h40 : 32'bz;  // Controlled_Buffer controlled_buffer_7
  assign pull_resistor_8_node = _8 ? 32'h80 : 32'bz;  // Controlled_Buffer controlled_buffer_8
  assign pull_resistor_9_node = _9 ? 32'h100 : 32'bz;  // Controlled_Buffer controlled_buffer_9
  assign pull_resistor_10_node = _10 ? 32'h200 : 32'bz;  // Controlled_Buffer controlled_buffer_10
  assign pull_resistor_11_node = _11 ? 32'h400 : 32'bz;  // Controlled_Buffer controlled_buffer_11
  assign pull_resistor_12_node = _12 ? 32'h800 : 32'bz;  // Controlled_Buffer controlled_buffer_12
  assign pull_resistor_13_node = _13 ? 32'h1000 : 32'bz;  // Controlled_Buffer controlled_buffer_13
  assign pull_resistor_14_node = _14 ? 32'h2000 : 32'bz;  // Controlled_Buffer controlled_buffer_14
  assign pull_resistor_15_node = _15 ? 32'h4000 : 32'bz;  // Controlled_Buffer controlled_buffer_15
  assign pull_resistor_16_node = _16 ? 32'h8000 : 32'bz;  // Controlled_Buffer controlled_buffer_16
  assign pull_resistor_17_node = _17 ? 32'h10000 : 32'bz;  // Controlled_Buffer controlled_buffer_17
  assign pull_resistor_18_node = _18 ? 32'h20000 : 32'bz;  // Controlled_Buffer controlled_buffer_18
  assign pull_resistor_19_node = _19 ? 32'h40000 : 32'bz;  // Controlled_Buffer controlled_buffer_19
  assign pull_resistor_20_node = _20 ? 32'h80000 : 32'bz;  // Controlled_Buffer controlled_buffer_20
  assign pull_resistor_21_node = _21 ? 32'h100000 : 32'bz;  // Controlled_Buffer controlled_buffer_21
  assign pull_resistor_22_node = _22 ? 32'h200000 : 32'bz;  // Controlled_Buffer controlled_buffer_22
  assign pull_resistor_23_node = _23 ? 32'h400000 : 32'bz;  // Controlled_Buffer controlled_buffer_23
  assign pull_resistor_24_node = _24 ? 32'h800000 : 32'bz;  // Controlled_Buffer controlled_buffer_24
  assign pull_resistor_25_node = _25 ? 32'h1000000 : 32'bz;  // Controlled_Buffer controlled_buffer_25
  assign pull_resistor_26_node = _26 ? 32'h2000000 : 32'bz;  // Controlled_Buffer controlled_buffer_26
  assign pull_resistor_27_node = _27 ? 32'h4000000 : 32'bz;  // Controlled_Buffer controlled_buffer_27
  assign pull_resistor_28_node = _28 ? 32'h8000000 : 32'bz;  // Controlled_Buffer controlled_buffer_28
  assign pull_resistor_29_node = _29 ? 32'h10000000 : 32'bz;  // Controlled_Buffer controlled_buffer_29
  assign pull_resistor_30_node = _30 ? 32'h20000000 : 32'bz;  // Controlled_Buffer controlled_buffer_30
  assign pull_resistor_31_node = _31 ? 32'h40000000 : 32'bz;  // Controlled_Buffer controlled_buffer_31
  assign pull_resistor_32_node = _32 ? 32'h80000000 : 32'bz;  // Controlled_Buffer controlled_buffer_32
  assign n1 = pull_resistor_1_node & colods;  // AND_Gate and_2, 32 bits wide
  assign n2 = pull_resistor_2_node & colods;  // AND_Gate and_3, 32 bits wide
  assign n3 = pull_resistor_3_node & colods;  // AND_Gate and_4, 32 bits wide
  assign n4 = pull_resistor_4_node & colods;  // AND_Gate and_5, 32 bits wide
  assign n5 = pull_resistor_5_node & colods;  // AND_Gate and_6, 32 bits wide
  assign n6 = pull_resistor_6_node & colods;  // AND_Gate and_7, 32 bits wide
  assign n7 = pull_resistor_7_node & colods;  // AND_Gate and_8, 32 bits wide
  assign n8 = pull_resistor_8_node & colods;  // AND_Gate and_9, 32 bits wide
  assign n9 = pull_resistor_9_node & colods;  // AND_Gate and_10, 32 bits wide
  assign n10 = pull_resistor_10_node & colods;  // AND_Gate and_11, 32 bits wide
  assign n11 = pull_resistor_11_node & colods;  // AND_Gate and_12, 32 bits wide
  assign n12 = pull_resistor_12_node & colods;  // AND_Gate and_13, 32 bits wide
  assign n13 = pull_resistor_13_node & colods;  // AND_Gate and_14, 32 bits wide
  assign n14 = pull_resistor_14_node & colods;  // AND_Gate and_15, 32 bits wide
  assign n15 = pull_resistor_15_node & colods;  // AND_Gate and_16, 32 bits wide
  assign n16 = pull_resistor_16_node & colods;  // AND_Gate and_17, 32 bits wide
  assign n17 = pull_resistor_17_node & colods;  // AND_Gate and_18, 32 bits wide
  assign n18 = pull_resistor_18_node & colods;  // AND_Gate and_19, 32 bits wide
  assign n19 = pull_resistor_19_node & colods;  // AND_Gate and_20, 32 bits wide
  assign n20 = pull_resistor_20_node & colods;  // AND_Gate and_21, 32 bits wide
  assign n21 = pull_resistor_21_node & colods;  // AND_Gate and_22, 32 bits wide
  assign n22 = pull_resistor_22_node & colods;  // AND_Gate and_23, 32 bits wide
  assign n23 = pull_resistor_23_node & colods;  // AND_Gate and_24, 32 bits wide
  assign n24 = pull_resistor_24_node & colods;  // AND_Gate and_25, 32 bits wide
  assign n25 = pull_resistor_25_node & colods;  // AND_Gate and_26, 32 bits wide
  assign n26 = pull_resistor_26_node & colods;  // AND_Gate and_27, 32 bits wide
  assign n27 = pull_resistor_27_node & colods;  // AND_Gate and_28, 32 bits wide
  assign n28 = pull_resistor_28_node & colods;  // AND_Gate and_29, 32 bits wide
  assign n29 = pull_resistor_29_node & colods;  // AND_Gate and_30, 32 bits wide
  assign n30 = pull_resistor_30_node & colods;  // AND_Gate and_31, 32 bits wide
  assign n31 = pull_resistor_31_node & colods;  // AND_Gate and_32, 32 bits wide
  assign n32 = pull_resistor_32_node & colods;  // AND_Gate and_33, 32 bits wide
  BitFinder #(.width(32)) bitfinder_1 (.in(n1), .found(bitfinder_1_found));  // open: index
  BitFinder #(.width(32)) bitfinder_2 (.in(n2), .found(bitfinder_2_found));  // open: index
  BitFinder #(.width(32)) bitfinder_3 (.in(n3), .found(bitfinder_3_found));  // open: index
  BitFinder #(.width(32)) bitfinder_4 (.in(n4), .found(bitfinder_4_found));  // open: index
  BitFinder #(.width(32)) bitfinder_5 (.in(n5), .found(bitfinder_5_found));  // open: index
  BitFinder #(.width(32)) bitfinder_6 (.in(n6), .found(bitfinder_6_found));  // open: index
  BitFinder #(.width(32)) bitfinder_7 (.in(n7), .found(bitfinder_7_found));  // open: index
  BitFinder #(.width(32)) bitfinder_8 (.in(n8), .found(bitfinder_8_found));  // open: index
  BitFinder #(.width(32)) bitfinder_9 (.in(n9), .found(bitfinder_9_found));  // open: index
  BitFinder #(.width(32)) bitfinder_10 (.in(n10), .found(bitfinder_10_found));  // open: index
  BitFinder #(.width(32)) bitfinder_11 (.in(n11), .found(bitfinder_11_found));  // open: index
  BitFinder #(.width(32)) bitfinder_12 (.in(n12), .found(bitfinder_12_found));  // open: index
  BitFinder #(.width(32)) bitfinder_13 (.in(n13), .found(bitfinder_13_found));  // open: index
  BitFinder #(.width(32)) bitfinder_14 (.in(n14), .found(bitfinder_14_found));  // open: index
  BitFinder #(.width(32)) bitfinder_15 (.in(n15), .found(bitfinder_15_found));  // open: index
  BitFinder #(.width(32)) bitfinder_16 (.in(n16), .found(bitfinder_16_found));  // open: index
  BitFinder #(.width(32)) bitfinder_17 (.in(n17), .found(bitfinder_17_found));  // open: index
  BitFinder #(.width(32)) bitfinder_18 (.in(n18), .found(bitfinder_18_found));  // open: index
  BitFinder #(.width(32)) bitfinder_19 (.in(n19), .found(bitfinder_19_found));  // open: index
  BitFinder #(.width(32)) bitfinder_20 (.in(n20), .found(bitfinder_20_found));  // open: index
  BitFinder #(.width(32)) bitfinder_21 (.in(n21), .found(bitfinder_21_found));  // open: index
  BitFinder #(.width(32)) bitfinder_22 (.in(n22), .found(bitfinder_22_found));  // open: index
  BitFinder #(.width(32)) bitfinder_23 (.in(n23), .found(bitfinder_23_found));  // open: index
  BitFinder #(.width(32)) bitfinder_24 (.in(n24), .found(bitfinder_24_found));  // open: index
  BitFinder #(.width(32)) bitfinder_25 (.in(n25), .found(bitfinder_25_found));  // open: index
  BitFinder #(.width(32)) bitfinder_26 (.in(n26), .found(bitfinder_26_found));  // open: index
  BitFinder #(.width(32)) bitfinder_27 (.in(n27), .found(bitfinder_27_found));  // open: index
  BitFinder #(.width(32)) bitfinder_28 (.in(n28), .found(bitfinder_28_found));  // open: index
  BitFinder #(.width(32)) bitfinder_29 (.in(n29), .found(bitfinder_29_found));  // open: index
  BitFinder #(.width(32)) bitfinder_30 (.in(n30), .found(bitfinder_30_found));  // open: index
  BitFinder #(.width(32)) bitfinder_31 (.in(n31), .found(bitfinder_31_found));  // open: index
  BitFinder #(.width(32)) bitfinder_32 (.in(n32), .found(bitfinder_32_found));  // open: index
  Pull_Resistor pull_resistor_33 (.node(pull_resistor_33_node));
  assign pull_resistor_33_node = bitfinder_1_found ? 4'b0010 : 4'bz;  // Controlled_Buffer controlled_buffer_33
  Pull_Resistor pull_resistor_34 (.node(pull_resistor_34_node));
  assign pull_resistor_34_node = bitfinder_2_found ? 4'b0011 : 4'bz;  // Controlled_Buffer controlled_buffer_34
  Pull_Resistor pull_resistor_35 (.node(pull_resistor_35_node));
  assign pull_resistor_35_node = bitfinder_3_found ? 4'b0100 : 4'bz;  // Controlled_Buffer controlled_buffer_35
  Pull_Resistor pull_resistor_36 (.node(pull_resistor_36_node));
  assign pull_resistor_36_node = bitfinder_4_found ? 4'b0101 : 4'bz;  // Controlled_Buffer controlled_buffer_36
  Pull_Resistor pull_resistor_37 (.node(pull_resistor_37_node));
  assign pull_resistor_37_node = bitfinder_5_found ? 4'b0110 : 4'bz;  // Controlled_Buffer controlled_buffer_37
  Pull_Resistor pull_resistor_38 (.node(pull_resistor_38_node));
  assign pull_resistor_38_node = bitfinder_6_found ? 4'b0111 : 4'bz;  // Controlled_Buffer controlled_buffer_38
  Pull_Resistor pull_resistor_39 (.node(pull_resistor_39_node));
  assign pull_resistor_39_node = bitfinder_7_found ? 4'b1000 : 4'bz;  // Controlled_Buffer controlled_buffer_39
  Pull_Resistor pull_resistor_40 (.node(pull_resistor_40_node));
  assign pull_resistor_40_node = bitfinder_8_found ? 4'b1001 : 4'bz;  // Controlled_Buffer controlled_buffer_40
  Pull_Resistor pull_resistor_41 (.node(pull_resistor_41_node));
  assign pull_resistor_41_node = bitfinder_9_found ? 4'b0010 : 4'bz;  // Controlled_Buffer controlled_buffer_41
  Pull_Resistor pull_resistor_42 (.node(pull_resistor_42_node));
  assign pull_resistor_42_node = bitfinder_10_found ? 4'b0011 : 4'bz;  // Controlled_Buffer controlled_buffer_42
  Pull_Resistor pull_resistor_43 (.node(pull_resistor_43_node));
  assign pull_resistor_43_node = bitfinder_11_found ? 4'b0100 : 4'bz;  // Controlled_Buffer controlled_buffer_43
  Pull_Resistor pull_resistor_44 (.node(pull_resistor_44_node));
  assign pull_resistor_44_node = bitfinder_12_found ? 4'b0101 : 4'bz;  // Controlled_Buffer controlled_buffer_44
  Pull_Resistor pull_resistor_45 (.node(pull_resistor_45_node));
  assign pull_resistor_45_node = bitfinder_13_found ? 4'b0110 : 4'bz;  // Controlled_Buffer controlled_buffer_45
  Pull_Resistor pull_resistor_46 (.node(pull_resistor_46_node));
  assign pull_resistor_46_node = bitfinder_14_found ? 4'b0111 : 4'bz;  // Controlled_Buffer controlled_buffer_46
  Pull_Resistor pull_resistor_47 (.node(pull_resistor_47_node));
  assign pull_resistor_47_node = bitfinder_15_found ? 4'b1000 : 4'bz;  // Controlled_Buffer controlled_buffer_47
  Pull_Resistor pull_resistor_48 (.node(pull_resistor_48_node));
  assign pull_resistor_48_node = bitfinder_16_found ? 4'b1001 : 4'bz;  // Controlled_Buffer controlled_buffer_48
  Pull_Resistor pull_resistor_49 (.node(pull_resistor_49_node));
  assign pull_resistor_49_node = bitfinder_17_found ? 4'b0010 : 4'bz;  // Controlled_Buffer controlled_buffer_49
  Pull_Resistor pull_resistor_50 (.node(pull_resistor_50_node));
  assign pull_resistor_50_node = bitfinder_18_found ? 4'b0011 : 4'bz;  // Controlled_Buffer controlled_buffer_50
  Pull_Resistor pull_resistor_51 (.node(pull_resistor_51_node));
  assign pull_resistor_51_node = bitfinder_19_found ? 4'b0100 : 4'bz;  // Controlled_Buffer controlled_buffer_51
  Pull_Resistor pull_resistor_52 (.node(pull_resistor_52_node));
  assign pull_resistor_52_node = bitfinder_20_found ? 4'b0101 : 4'bz;  // Controlled_Buffer controlled_buffer_52
  Pull_Resistor pull_resistor_53 (.node(pull_resistor_53_node));
  assign pull_resistor_53_node = bitfinder_21_found ? 4'b0110 : 4'bz;  // Controlled_Buffer controlled_buffer_53
  Pull_Resistor pull_resistor_54 (.node(pull_resistor_54_node));
  assign pull_resistor_54_node = bitfinder_22_found ? 4'b0111 : 4'bz;  // Controlled_Buffer controlled_buffer_54
  Pull_Resistor pull_resistor_55 (.node(pull_resistor_55_node));
  assign pull_resistor_55_node = bitfinder_23_found ? 4'b1000 : 4'bz;  // Controlled_Buffer controlled_buffer_55
  Pull_Resistor pull_resistor_56 (.node(pull_resistor_56_node));
  assign pull_resistor_56_node = bitfinder_24_found ? 4'b1001 : 4'bz;  // Controlled_Buffer controlled_buffer_56
  Pull_Resistor pull_resistor_57 (.node(pull_resistor_57_node));
  assign pull_resistor_57_node = bitfinder_25_found ? 4'b0010 : 4'bz;  // Controlled_Buffer controlled_buffer_57
  Pull_Resistor pull_resistor_58 (.node(pull_resistor_58_node));
  assign pull_resistor_58_node = bitfinder_26_found ? 4'b0011 : 4'bz;  // Controlled_Buffer controlled_buffer_58
  Pull_Resistor pull_resistor_59 (.node(pull_resistor_59_node));
  assign pull_resistor_59_node = bitfinder_27_found ? 4'b0100 : 4'bz;  // Controlled_Buffer controlled_buffer_59
  Pull_Resistor pull_resistor_60 (.node(pull_resistor_60_node));
  assign pull_resistor_60_node = bitfinder_28_found ? 4'b0101 : 4'bz;  // Controlled_Buffer controlled_buffer_60
  Pull_Resistor pull_resistor_61 (.node(pull_resistor_61_node));
  assign pull_resistor_61_node = bitfinder_29_found ? 4'b0110 : 4'bz;  // Controlled_Buffer controlled_buffer_61
  Pull_Resistor pull_resistor_62 (.node(pull_resistor_62_node));
  assign pull_resistor_62_node = bitfinder_30_found ? 4'b0111 : 4'bz;  // Controlled_Buffer controlled_buffer_62
  Pull_Resistor pull_resistor_63 (.node(pull_resistor_63_node));
  assign pull_resistor_63_node = bitfinder_31_found ? 4'b1000 : 4'bz;  // Controlled_Buffer controlled_buffer_63
  Pull_Resistor pull_resistor_64 (.node(pull_resistor_64_node));
  assign pull_resistor_64_node = bitfinder_32_found ? 4'b1001 : 4'bz;  // Controlled_Buffer controlled_buffer_64
  assign card = pull_resistor_33_node | pull_resistor_34_node | pull_resistor_35_node | pull_resistor_36_node | pull_resistor_37_node | pull_resistor_38_node | pull_resistor_39_node | pull_resistor_40_node | pull_resistor_41_node | pull_resistor_42_node | pull_resistor_43_node | pull_resistor_44_node | pull_resistor_45_node | pull_resistor_46_node | pull_resistor_47_node | pull_resistor_48_node | pull_resistor_49_node | pull_resistor_50_node | pull_resistor_51_node | pull_resistor_52_node | pull_resistor_53_node | pull_resistor_54_node | pull_resistor_55_node | pull_resistor_56_node | pull_resistor_57_node | pull_resistor_58_node | pull_resistor_59_node | pull_resistor_60_node | pull_resistor_61_node | pull_resistor_62_node | pull_resistor_63_node | pull_resistor_64_node;  // OR_Gate or_1, 4 bits wide
endmodule

module generator (
  input  clock,
  input  reset,
  output [7:0] address,
  output [7:0] data,
  output l_d,
  output clock_gen,
  output gen_done
);

  wire bitfinder_1_found, comparator_1_eq, comparator_2_eq, comparator_3_eq, comparator_4_eq,
       comparator_5_eq, comparator_6_eq, comparator_7_eq, comparator_8_gt, comparator_9_eq, comparator_10_eq,
       comparator_12_eq, eq_0, gen_done_t, not_1_out, not_2_out, not_3_out, not_4_out, not_5_out, or_1_out,
       or_2_out, tact;
  wire [3:0] configuration_1_card;
  wire [4:0] adder_1_out, multiplexer_2_out, register_1_q;
  wire [7:0] addr, counter_1_q, counter_2_q;
  wire [7:7] pull_resistor_1_node;
  wire [31:0] configuration_1_final_colod, multiplexer_3_out, multiplexer_4_out, pull_resistor_2_node;

  Multiplexer #(.select(5), .width(8), .disabled(0), .enable("false")) multiplexer_1 (
    .in0(8'h91), .in1(8'h92), .in2(8'h9a), .in3(8'h9b), .in4(8'h9c), .in5(8'ha4), .in6(8'ha5), .in7(8'ha6),
    .in8(8'ha7), .in9(8'haf), .in10(8'hb0), .in11(8'hb1), .in12(8'hb2), .in13(8'hb3), .in14(8'hbb),
    .in15(8'hbc), .in16(8'hbd), .in17(8'hbe), .in18(8'hbf), .in19(8'hc8), .in20(8'hc9), .in21(8'hca),
    .in22(8'hcb), .in23(8'hcc), .in24(8'hcd), .in25(8'hd6), .in26(8'hd7), .in27(8'hd8), .in28(8'hd9),
    .in29(8'hda), .in30(8'hdb), .in31(8'hdc), .out(addr), .sel(register_1_q));
  Multiplexer #(.width(5), .enable("false")) multiplexer_2 (
    .in0({5{1'b0}}), .in1(adder_1_out), .out(multiplexer_2_out), .sel(comparator_8_gt));
  and and_1 (tact, clock, gen_done_t);
  Adder #(.width(5)) adder_1 (.a(register_1_q), .b(5'b00001), .out(adder_1_out));  // open: cin, cout
  not not_1 (not_1_out, eq_0);
  Counter counter_1 (.D({8{1'b0}}), .Q(counter_1_q), .clk(tact), .clr(reset));  // open: load, count, carry
  Comparator comparator_1 (.a(8'h92), .b(addr), .eq(comparator_1_eq));  // open: gt, lt
  Comparator comparator_2 (.a(8'h9c), .b(addr), .eq(comparator_2_eq));  // open: gt, lt
  Comparator comparator_3 (.a(8'ha7), .b(addr), .eq(comparator_3_eq));  // open: gt, lt
  Comparator comparator_4 (.a(8'hb3), .b(addr), .eq(comparator_4_eq));  // open: gt, lt
  Comparator comparator_5 (.a(8'hbf), .b(addr), .eq(comparator_5_eq));  // open: gt, lt
  Comparator comparator_6 (.a(8'hcd), .b(addr), .eq(comparator_6_eq));  // open: gt, lt
  Comparator comparator_7 (.a(8'hdc), .b(addr), .eq(comparator_7_eq));  // open: gt, lt
  Register #(.width(5)) register_1 (
    .D(multiplexer_2_out), .en(not_1_out), .Q(register_1_q), .clk(not_2_out), .clr(reset));
  not not_2 (not_2_out, tact);
  Comparator #(.mode("unsigned")) comparator_8 (.a(counter_1_q), .b({8{1'b0}}), .gt(comparator_8_gt));  // open: eq, lt
  or or_1 (or_1_out, gen_done_t, comparator_9_eq);
  or or_2 (or_2_out, comparator_1_eq, comparator_2_eq, comparator_3_eq, comparator_4_eq, comparator_5_eq, comparator_6_eq, comparator_7_eq);
  Multiplexer #(.width(32)) multiplexer_3 (
    .in0({32{1'b1}}), .in1(multiplexer_4_out), .out(multiplexer_3_out), .sel(not_3_out));  // open: en
  Counter counter_2 (.Q(counter_2_q), .clk(tact), .clr(reset));  // open: load, D, count, carry
  assign address = or_1_out ? addr : 8'bz;  // Controlled_Buffer controlled_buffer_1
  Comparator #(.mode("unsigned")) comparator_9 (.a(8'hdc), .b(addr), .eq(comparator_9_eq));  // open: gt, lt
  Pull_Resistor #(.pull(1)) pull_resistor_1 (.node(pull_resistor_1_node[7]));
  assign pull_resistor_1_node[7] = or_2_out ? 1'b0 : 1'bz;  // Controlled_Buffer controlled_buffer_2
  Pull_Resistor #(.pull(1)) pull_resistor_2 (.node(pull_resistor_2_node));
  assign pull_resistor_2_node = bitfinder_1_found ? multiplexer_3_out : 32'bz;  // Controlled_Buffer controlled_buffer_3
  not not_3 (not_3_out, comparator_10_eq);
  Comparator #(.mode("unsigned")) comparator_10 (
    .a({8{1'b0}}), .b(counter_2_q), .eq(comparator_10_eq));  // open: gt, lt
  BitFinder bitfinder_1 (.in(counter_2_q), .found(bitfinder_1_found));  // open: index
  configuration configuration_1 (
    .colods(pull_resistor_2_node), .clock(clock), .card(configuration_1_card),
    .final_colod(configuration_1_final_colod));
  Multiplexer #(.width(32), .enable("false")) multiplexer_4 (
    .in0(pull_resistor_2_node), .in1(configuration_1_final_colod), .out(multiplexer_4_out), .sel(not_4_out));
  not not_4 (not_4_out, clock);
  assign l_d = gen_done_t ? eq_0 : 1'bz;  // Controlled_Buffer controlled_buffer_4
  assign clock_gen = gen_done_t ? not_5_out : 1'bz;  // Controlled_Buffer controlled_buffer_5
  not not_5 (not_5_out, clock);
  Hex_Digit_Display hex_digit_display_1 (.value(configuration_1_card));  // open: dp
  assign data = gen_done_t ? {pull_resistor_1_node[7], 3'b100, configuration_1_card} : 8'bz;  // Controlled_Buffer controlled_buffer_6
  Comparator #(.width(4)) comparator_11 (.a(4'b0000), .b(configuration_1_card), .eq(eq_0));  // open: gt, lt
  Comparator #(.width(32)) comparator_12 (
    .a({32{1'b0}}), .b(multiplexer_4_out), .eq(comparator_12_eq));  // open: gt, lt
  not not_6 (gen_done, gen_done_t);
  not not_7 (gen_done_t, comparator_12_eq);

  // Notes on the sheet:
  //   1 colon
  //   2 colon
  //   3 colon
  //   4 colon
  //   5 colon
  //   6 colon
  //   7 colon
  //   opened
  //   sentinels
  //   Chooses random card from colod
endmodule

module write_sentinels (
  input  clock,
  input  reset,
  output [7:0] address,
  output [7:0] data,
  output l_d,
  output clock_gen,
  output sent_writing_done
);

  wire comparator_1_gt, gen_done, not_1_out, not_2_out, tact;
  wire [2:0] adder_1_out, multiplexer_2_out, register_1_q;
  wire [7:0] addr, counter_1_q;

  Multiplexer #(.select(3), .width(8), .disabled(0), .enable("false")) multiplexer_1 (
    .in0(8'h90), .in1(8'h99), .in2(8'ha3), .in3(8'hae), .in4(8'hba), .in5(8'hc7), .in6(8'hd5),
    .in7({8{1'b1}}), .out(addr), .sel(register_1_q));
  Multiplexer #(.width(3), .enable("false")) multiplexer_2 (
    .in0(3'b000), .in1(adder_1_out), .out(multiplexer_2_out), .sel(comparator_1_gt));
  Counter counter_1 (.D({8{1'b0}}), .Q(counter_1_q), .clk(tact), .clr(reset));  // open: load, count, carry
  assign address = gen_done ? addr : 8'bz;  // Controlled_Buffer controlled_buffer_1
  Adder #(.width(3)) adder_1 (.a(register_1_q), .b(3'b001), .out(adder_1_out));  // open: cin, cout
  Register #(.width(3)) register_1 (
    .D(multiplexer_2_out), .en(gen_done), .Q(register_1_q), .clk(not_1_out), .clr(reset));
  not not_1 (not_1_out, tact);
  Comparator #(.mode("unsigned")) comparator_1 (.a(counter_1_q), .b({8{1'b0}}), .gt(comparator_1_gt));  // open: eq, lt
  assign l_d = gen_done ? 1'b0 : 1'bz;  // Controlled_Buffer controlled_buffer_2
  assign clock_gen = gen_done ? not_2_out : 1'bz;  // Controlled_Buffer controlled_buffer_3
  not not_2 (not_2_out, clock);
  assign data = gen_done ? 8'ha : 8'bz;  // Controlled_Buffer controlled_buffer_4
  Comparator #(.mode("unsigned")) comparator_2 (.a({8{1'b1}}), .b(addr), .eq(sent_writing_done));  // open: gt, lt
  and and_1 (tact, clock, gen_done);
  not not_3 (gen_done, sent_writing_done);

  // Notes on the sheet:
  //   opened
  //   sentinels
endmodule

module card_replace (
  input  [2:0] colod_number,
  input  [7:0] cur_command,
  output [7:0] updated_program,
  output move_done_updated
);

  wire _1st_done, _2st_done, and_1_out, and_2_out, and_3_out, and_4_out, and_5_out, and_6_out, and_7_out,
       and_8_out, colod_isnt_0, comparator_1_eq, not_equal, or_3_out, or_4_out;

  Comparator #(.width(3), .mode("unsigned")) comparator_1 (
    .a(colod_number), .b(3'b000), .eq(comparator_1_eq));  // open: gt, lt
  not not_1 (colod_isnt_0, comparator_1_eq);
  Comparator #(.width(3), .mode("unsigned")) comparator_2 (
    .a(colod_number), .b(cur_command[2:0]), .eq(not_equal));  // open: gt, lt
  or or_1 (_1st_done, cur_command[0], cur_command[1], cur_command[2], cur_command[3]);
  or or_2 (_2st_done, cur_command[4], cur_command[5], cur_command[6], cur_command[7]);
  and and_1 (and_1_out, _1st_done, _2st_done);
  or or_3 (or_3_out, updated_program[0], updated_program[1], updated_program[2], updated_program[3]);
  and and_2 (and_2_out, or_3_out, or_4_out);
  or or_4 (or_4_out, updated_program[4], updated_program[5], updated_program[6], updated_program[7]);
  or or_5 (move_done_updated, and_1_out, and_2_out);
  and and_3 (and_3_out, _1st_done, colod_isnt_0, _2st_done, ~not_equal);  // AND_Gate
  and and_4 (and_4_out, _1st_done, ~colod_isnt_0, _2st_done, ~not_equal);  // AND_Gate
  and and_5 (and_5_out, _1st_done, colod_isnt_0, ~_2st_done, ~not_equal);  // AND_Gate
  and and_6 (and_6_out, ~_1st_done, colod_isnt_0, ~_2st_done, ~not_equal);  // AND_Gate
  and and_7 (and_7_out, _1st_done, ~colod_isnt_0, ~_2st_done, ~not_equal);  // AND_Gate
  and and_8 (and_8_out, ~_1st_done, ~colod_isnt_0, ~_2st_done, ~not_equal);  // AND_Gate
  assign updated_program = and_3_out ? cur_command : 8'bz;  // Controlled_Buffer controlled_buffer_1
  assign updated_program = and_4_out ? cur_command : 8'bz;  // Controlled_Buffer controlled_buffer_2
  assign updated_program = and_5_out ? {1'b0, colod_number, cur_command[3:0]} : 8'bz;  // Controlled_Buffer controlled_buffer_3
  assign updated_program = and_6_out ? {cur_command[7:4], 1'b0, colod_number} : 8'bz;  // Controlled_Buffer controlled_buffer_4
  assign updated_program = and_7_out ? cur_command : 8'bz;  // Controlled_Buffer controlled_buffer_5
  assign updated_program = and_8_out ? cur_command : 8'bz;  // Controlled_Buffer controlled_buffer_6
  assign updated_program = not_equal ? cur_command : 8'bz;  // Controlled_Buffer controlled_buffer_7

  // Other names for the same wires on the sheet: c[2:0] = colod_number;
  //   case1 (some bits) = {cur_command[7:4], colod_number}; case2[6:0] = {colod_number, cur_command[3:0]};
  //   case3[7:0] = cur_command; command[7:0] = cur_command; res[7:0] = updated_program
endmodule

module print_cards (
  input  clock,
  input  move_done,
  output [7:0] adr,
  output print
);

  wire pull_resistor_1_node;
  wire [7:0] adr_t;

  Counter counter_1 (.Q(adr_t), .clk(pull_resistor_1_node), .clr(move_done));  // open: load, D, count, carry
  Pull_Resistor pull_resistor_1 (.node(pull_resistor_1_node));
  assign pull_resistor_1_node = print ? clock : 1'bz;  // Controlled_Buffer controlled_buffer_1
  Comparator comparator_1 (.a(adr_t), .b(8'h4d), .lt(print));  // open: gt, eq
  ROM rom_1 (.addr(adr_t), .data(adr));  // open: sel

  // Notes on the sheet:
  //   sentinels
  //   cards
  //   contents of rom_1 (hex, n*v repeats v):
  //   90 91 92 93 94 95 96 97 98 9a 9b 9c 9d 9e 9f a0 a1 a2 a4 a5 a6 a7 a8 a9 aa ab ac ad af b0 b1 b2 b3
  //   b4 b5 b6 b7 b8 b9 bb bc bd be bf c0 c1 c2 c3 c4 c5 c6 c8 c9 ca cb cc cd ce cf d0 d1 d2 d3 d4 d6 d7
  //   d8 d9 da db dc dd de df e0 e1 e2 e3 e4
endmodule
