// Logisim project 2_clean.circ as structural Verilog: 6 circuits, main circuit main
module main (
);

  wire _1colod, _2colod, _3colod, _4colod, _5colod, _6colod, _7colod, and_1_out, and_4_out, and_7_out,
       and_8_out, and_9_out, and_10_out, cancel_com, cdm8_done, cdm_8_mark5_1_p3, cdm_8_mark5_1_p5, Clock,
       com_written, command_clock, command_ld, comparator_1_eq, comparator_2_eq, comparator_3_eq,
       comparator_4_eq, comparator_5_eq, comparator_6_eq, comparator_7_eq, comparator_8_eq, comparator_9_eq,
       comparator_10_eq, comparator_11_eq, comparator_12_eq, comparator_13_eq, comparator_14_eq,
       comparator_15_eq, comparator_16_eq, comparator_17_eq, comparator_18_eq, comparator_19_eq,
       comparator_20_eq, comparator_21_eq, comparator_22_eq, comparator_23_eq, comparator_24_eq,
       comparator_25_eq, comparator_26_eq, comparator_27_eq, comparator_28_eq, comparator_29_eq,
       comparator_30_eq, comparator_31_eq, comparator_32_eq, comparator_33_eq, comparator_34_eq,
       comparator_35_eq, comparator_36_eq, comparator_37_eq, comparator_38_eq, comparator_39_eq,
       comparator_40_eq, comparator_41_eq, comparator_42_eq, comparator_43_eq, comparator_44_eq,
       comparator_45_eq, comparator_46_eq, comparator_47_eq, comparator_48_eq, comparator_49_eq,
       comparator_50_eq, comparator_51_eq, comparator_52_eq, comparator_53_eq, comparator_54_eq,
       comparator_55_eq, comparator_56_eq, comparator_57_eq, comparator_58_eq, comparator_59_eq,
       comparator_60_eq, comparator_61_eq, comparator_62_eq, comparator_63_eq, comparator_65_eq,
       comparator_66_eq, comparator_67_eq, comparator_68_eq, comparator_69_eq, comparator_70_eq,
       comparator_71_eq, comparator_72_eq, comparator_73_eq, comparator_74_eq, comparator_75_eq,
       comparator_76_eq, comparator_77_eq, comparator_78_eq, controlled_buffer_3_out, d_ff_1_q, d_ff_4_q,
       data_ins, data_o, do_prog, first_usage, gen_done, gen_ld, ins_p, IO_o, memory, move_done, new_com,
       not_1_out, not_2_out, not_3_out, not_4_out, not_5_out, not_6_out, not_7_out, or_2_out, or_3_out,
       or_4_out, or_6_out, print_cards_1_print, print_ld, pull_resistor_3_node, RAM_r_wr_prime, RAM_sel,
       read_write, reset, run_com, sent_done, shocetake, to_print, vector_p, zeroing;
  wire [0:0] and_2_out;
  wire [2:0] priority_encoder_1_out;
  wire [3:0] _9a, _9b, _9c, _9d, _9e, _9f, _91, _92, _93, _94, _95, _96, _97, _98, a0, a1, a2, a4, a5, a6,
       a7, a8, a9, aa, ab, ac, ad, af, b0, b1, b2, b3, b4, b5, b6, b7, b8, b9, bb, bc, bd, be, bf, c0, c1,
       c2, c3, c4, c5, c6, c8, c9, ca, cb, cc, cd, ce, cf, d0, d1, d2, d3, d4, d6, d7, d8, d9, da, db, dc,
       dd, de, df, e0, e1, e2, e3, value;
  wire [7:0] addr, card_address, card_value, cdm_8_mark5_1_p10, cdm_8_mark5_1_p11, command_address,
       command_data, counter_1_q, counter_2_q, current_command, data_base, gen_data, multiplexer_4_out,
       multiplexer_5_out, print_cards_1_adr, RAM_address, register_79_q;

  Button button_1 ();  // open: out
  D_Flip_Flop d_ff_1 (.Q(d_ff_1_q), .preset(do_prog), .reset(and_1_out));  // open: clk, D, Qn, en
  and and_1 (and_1_out, not_2_out, not_1_out);
  not not_1 (not_1_out, not_2_out);
  and and_2 (and_2_out[0], addr[4], addr[5], addr[6], addr[7]);
  Comparator comparator_1 (.a(card_address), .b(8'h91), .eq(comparator_1_eq));  // open: gt, lt
  Comparator comparator_2 (.a(card_address), .b(8'h92), .eq(comparator_2_eq));  // open: gt, lt
  Comparator comparator_3 (.a(card_address), .b(8'h93), .eq(comparator_3_eq));  // open: gt, lt
  Comparator comparator_4 (.a(card_address), .b(8'h94), .eq(comparator_4_eq));  // open: gt, lt
  Comparator comparator_5 (.a(card_address), .b(8'h95), .eq(comparator_5_eq));  // open: gt, lt
  Comparator comparator_6 (.a(card_address), .b(8'h96), .eq(comparator_6_eq));  // open: gt, lt
  Comparator comparator_7 (.a(card_address), .b(8'h97), .eq(comparator_7_eq));  // open: gt, lt
  Comparator comparator_8 (.a(card_address), .b(8'h98), .eq(comparator_8_eq));  // open: gt, lt
  // Probe on cdm_8_mark5_1_p3
  // NOT_Gate not_2 has open pins: in=open, out=not_2_out
  Decoder #(.select(2), .disabled(0)) decoder_1 (
    .out0(ins_p), .out1(vector_p), .out2(data_o), .out3(IO_o), .sel({data_ins, and_2_out[0]}), .en(memory));
  or or_1 (RAM_sel, gen_ld, not_3_out);
  not not_3 (not_3_out, read_write);
  and and_3 (RAM_r_wr_prime, read_write, ~gen_ld);  // AND_Gate
  Multiplexer #(.width(8), .enable("false")) multiplexer_1 (
    .in0(addr), .in1(command_address), .out(RAM_address), .sel(gen_ld));
  Multiplexer #(.width(8), .enable("false")) multiplexer_2 (
    .in0(data_base), .in1(gen_data), .out(card_value), .sel(gen_ld));
  Multiplexer #(.width(4), .enable("false")) multiplexer_3 (
    .in0(card_value[3:0]), .in1(4'b1100), .out(value), .sel(card_value[7]));
  Register #(.width(4)) register_1 (.D(value), .Q(_91), .clk(comparator_1_eq));  // open: en, clr
  Register #(.width(4)) register_2 (.D(value), .Q(_92), .clk(comparator_2_eq));  // open: en, clr
  Register #(.width(4)) register_3 (.D(value), .Q(_93), .clk(comparator_3_eq));  // open: en, clr
  Register #(.width(4)) register_4 (.D(value), .Q(_94), .clk(comparator_4_eq));  // open: en, clr
  Register #(.width(4)) register_5 (.D(value), .Q(_95), .clk(comparator_5_eq));  // open: en, clr
  Register #(.width(4)) register_6 (.D(value), .Q(_96), .clk(comparator_6_eq));  // open: en, clr
  Register #(.width(4)) register_7 (.D(value), .Q(_97), .clk(comparator_7_eq));  // open: en, clr
  Register #(.width(4)) register_8 (.D(value), .Q(_98), .clk(comparator_8_eq));  // open: en, clr
  // Probe on cdm_8_mark5_1_p5
  Clock clock_1 (.out(Clock));
  Comparator comparator_9 (.a(card_address), .b(8'h9a), .eq(comparator_9_eq));  // open: gt, lt
  Comparator comparator_10 (.a(card_address), .b(8'h9b), .eq(comparator_10_eq));  // open: gt, lt
  Comparator comparator_11 (.a(card_address), .b(8'h9c), .eq(comparator_11_eq));  // open: gt, lt
  Comparator comparator_12 (.a(card_address), .b(8'h9d), .eq(comparator_12_eq));  // open: gt, lt
  Comparator comparator_13 (.a(card_address), .b(8'h9e), .eq(comparator_13_eq));  // open: gt, lt
  Comparator comparator_14 (.a(card_address), .b(8'h9f), .eq(comparator_14_eq));  // open: gt, lt
  Comparator comparator_15 (.a(card_address), .b(8'ha0), .eq(comparator_15_eq));  // open: gt, lt
  Comparator comparator_16 (.a(card_address), .b(8'ha1), .eq(comparator_16_eq));  // open: gt, lt
  Comparator comparator_17 (.a(card_address), .b(8'ha2), .eq(comparator_17_eq));  // open: gt, lt
  // CdM_8_mark5 cdm_8_mark5_1: pin names not known; wires that end beside it: d_ff_1_q, 3'b000, cdm_8_mark5_1_p3, Clock, cdm_8_mark5_1_p5, data_ins, memory, read_write, addr, cdm_8_mark5_1_p10, cdm_8_mark5_1_p11
  not not_4 (not_4_out, read_write);
  assign cdm_8_mark5_1_p11 = read_write ? data_base : 8'bz;  // Controlled_Buffer controlled_buffer_1
  Register #(.width(4)) register_9 (.D(value), .Q(_9a), .clk(comparator_9_eq));  // open: en, clr
  Register #(.width(4)) register_10 (.D(value), .Q(_9b), .clk(comparator_10_eq));  // open: en, clr
  Register #(.width(4)) register_11 (.D(value), .Q(_9c), .clk(comparator_11_eq));  // open: en, clr
  Register #(.width(4)) register_12 (.D(value), .Q(_9d), .clk(comparator_12_eq));  // open: en, clr
  Register #(.width(4)) register_13 (.D(value), .Q(_9e), .clk(comparator_13_eq));  // open: en, clr
  Register #(.width(4)) register_14 (.D(value), .Q(_9f), .clk(comparator_14_eq));  // open: en, clr
  Register #(.width(4)) register_15 (.D(value), .Q(a0), .clk(comparator_15_eq));  // open: en, clr
  Register #(.width(4)) register_16 (.D(value), .Q(a1), .clk(comparator_16_eq));  // open: en, clr
  Register #(.width(4)) register_17 (.D(value), .Q(a2), .clk(comparator_17_eq));  // open: en, clr
  assign data_base = not_4_out ? cdm_8_mark5_1_p10 : 8'bz;  // Controlled_Buffer controlled_buffer_2
  // Probe on RAM_address
  Register #(.width(4)) register_18 (.D(value), .Q(a4), .clk(comparator_18_eq));  // open: en, clr
  Comparator comparator_18 (.a(card_address), .b(8'ha4), .eq(comparator_18_eq));  // open: gt, lt
  Register #(.width(4)) register_19 (.D(value), .Q(a5), .clk(comparator_19_eq));  // open: en, clr
  Comparator comparator_19 (.a(card_address), .b(8'ha5), .eq(comparator_19_eq));  // open: gt, lt
  Register #(.width(4)) register_20 (.D(value), .Q(a6), .clk(comparator_20_eq));  // open: en, clr
  Comparator comparator_20 (.a(card_address), .b(8'ha6), .eq(comparator_20_eq));  // open: gt, lt
  Register #(.width(4)) register_21 (.D(value), .Q(a7), .clk(comparator_21_eq));  // open: en, clr
  Comparator comparator_21 (.a(card_address), .b(8'ha7), .eq(comparator_21_eq));  // open: gt, lt
  Register #(.width(4)) register_22 (.D(value), .Q(a8), .clk(comparator_22_eq));  // open: en, clr
  Comparator comparator_22 (.a(card_address), .b(8'ha8), .eq(comparator_22_eq));  // open: gt, lt
  Register #(.width(4)) register_23 (.D(value), .Q(a9), .clk(comparator_23_eq));  // open: en, clr
  Comparator comparator_23 (.a(card_address), .b(8'ha9), .eq(comparator_23_eq));  // open: gt, lt
  Register #(.width(4)) register_24 (.D(value), .Q(aa), .clk(comparator_24_eq));  // open: en, clr
  Comparator comparator_24 (.a(card_address), .b(8'haa), .eq(comparator_24_eq));  // open: gt, lt
  Register #(.width(4)) register_25 (.D(value), .Q(ab), .clk(comparator_25_eq));  // open: en, clr
  Comparator comparator_25 (.a(card_address), .b(8'hab), .eq(comparator_25_eq));  // open: gt, lt
  Register #(.width(4)) register_26 (.D(value), .Q(ac), .clk(comparator_26_eq));  // open: en, clr
  Comparator comparator_26 (.a(card_address), .b(8'hac), .eq(comparator_26_eq));  // open: gt, lt
  Register #(.width(4)) register_27 (.D(value), .Q(ad), .clk(comparator_27_eq));  // open: en, clr
  Comparator comparator_27 (.a(card_address), .b(8'had), .eq(comparator_27_eq));  // open: gt, lt
  not not_5 (not_5_out, Clock);
  Pull_Resistor pull_resistor_1 (.node(gen_ld));
  and and_4 (and_4_out, or_2_out, shocetake);
  or or_2 (or_2_out, ins_p, vector_p);
  RAM ram_1 (.addr(RAM_address), .data(card_value), .sel(RAM_sel), .clk(not_5_out), .ld(RAM_r_wr_prime), .clr(reset));
  // Probe on card_value
  Register #(.width(4)) register_28 (.D(value), .Q(af), .clk(comparator_28_eq));  // open: en, clr
  Comparator comparator_28 (.a(card_address), .b(8'haf), .eq(comparator_28_eq));  // open: gt, lt
  Register #(.width(4)) register_29 (.D(value), .Q(b0), .clk(comparator_29_eq));  // open: en, clr
  Comparator comparator_29 (.a(card_address), .b(8'hb0), .eq(comparator_29_eq));  // open: gt, lt
  Register #(.width(4)) register_30 (.D(value), .Q(b1), .clk(comparator_30_eq));  // open: en, clr
  Comparator comparator_30 (.a(card_address), .b(8'hb1), .eq(comparator_30_eq));  // open: gt, lt
  Register #(.width(4)) register_31 (.D(value), .Q(b2), .clk(comparator_31_eq));  // open: en, clr
  Comparator comparator_31 (.a(card_address), .b(8'hb2), .eq(comparator_31_eq));  // open: gt, lt
  Register #(.width(4)) register_32 (.D(value), .Q(b3), .clk(comparator_32_eq));  // open: en, clr
  Comparator comparator_32 (.a(card_address), .b(8'hb3), .eq(comparator_32_eq));  // open: gt, lt
  Register #(.width(4)) register_33 (.D(value), .Q(b4), .clk(comparator_33_eq));  // open: en, clr
  Comparator comparator_33 (.a(card_address), .b(8'hb4), .eq(comparator_33_eq));  // open: gt, lt
  Register #(.width(4)) register_34 (.D(value), .Q(b5), .clk(comparator_34_eq));  // open: en, clr
  Comparator comparator_34 (.a(card_address), .b(8'hb5), .eq(comparator_34_eq));  // open: gt, lt
  Register #(.width(4)) register_35 (.D(value), .Q(b6), .clk(comparator_35_eq));  // open: en, clr
  Comparator comparator_35 (.a(card_address), .b(8'hb6), .eq(comparator_35_eq));  // open: gt, lt
  Register #(.width(4)) register_36 (.D(value), .Q(b7), .clk(comparator_36_eq));  // open: en, clr
  Comparator comparator_36 (.a(card_address), .b(8'hb7), .eq(comparator_36_eq));  // open: gt, lt
  Register #(.width(4)) register_37 (.D(value), .Q(b8), .clk(comparator_37_eq));  // open: en, clr
  Comparator comparator_37 (.a(card_address), .b(8'hb8), .eq(comparator_37_eq));  // open: gt, lt
  Register #(.width(4)) register_38 (.D(value), .Q(b9), .clk(comparator_38_eq));  // open: en, clr
  Comparator comparator_38 (.a(card_address), .b(8'hb9), .eq(comparator_38_eq));  // open: gt, lt
  ROM rom_1 (.addr(addr), .data(data_base), .sel(and_4_out));
  Comparator comparator_39 (.a(card_address), .b(8'hbb), .eq(comparator_39_eq));  // open: gt, lt
  Comparator comparator_40 (.a(card_address), .b(8'hbc), .eq(comparator_40_eq));  // open: gt, lt
  Comparator comparator_41 (.a(card_address), .b(8'hbd), .eq(comparator_41_eq));  // open: gt, lt
  Comparator comparator_42 (.a(card_address), .b(8'hbe), .eq(comparator_42_eq));  // open: gt, lt
  Comparator comparator_43 (.a(card_address), .b(8'hbf), .eq(comparator_43_eq));  // open: gt, lt
  Comparator comparator_44 (.a(card_address), .b(8'hc0), .eq(comparator_44_eq));  // open: gt, lt
  Comparator comparator_45 (.a(card_address), .b(8'hc1), .eq(comparator_45_eq));  // open: gt, lt
  Comparator comparator_46 (.a(card_address), .b(8'hc2), .eq(comparator_46_eq));  // open: gt, lt
  Comparator comparator_47 (.a(card_address), .b(8'hc3), .eq(comparator_47_eq));  // open: gt, lt
  Comparator comparator_48 (.a(card_address), .b(8'hc4), .eq(comparator_48_eq));  // open: gt, lt
  Comparator comparator_49 (.a(card_address), .b(8'hc5), .eq(comparator_49_eq));  // open: gt, lt
  Comparator comparator_50 (.a(card_address), .b(8'hc6), .eq(comparator_50_eq));  // open: gt, lt
  Register #(.width(4)) register_39 (.D(value), .Q(bb), .clk(comparator_39_eq));  // open: en, clr
  Register #(.width(4)) register_40 (.D(value), .Q(bc), .clk(comparator_40_eq));  // open: en, clr
  Register #(.width(4)) register_41 (.D(value), .Q(bd), .clk(comparator_41_eq));  // open: en, clr
  Register #(.width(4)) register_42 (.D(value), .Q(be), .clk(comparator_42_eq));  // open: en, clr
  Register #(.width(4)) register_43 (.D(value), .Q(bf), .clk(comparator_43_eq));  // open: en, clr
  Register #(.width(4)) register_44 (.D(value), .Q(c0), .clk(comparator_44_eq));  // open: en, clr
  Register #(.width(4)) register_45 (.D(value), .Q(c1), .clk(comparator_45_eq));  // open: en, clr
  Register #(.width(4)) register_46 (.D(value), .Q(c2), .clk(comparator_46_eq));  // open: en, clr
  Register #(.width(4)) register_47 (.D(value), .Q(c3), .clk(comparator_47_eq));  // open: en, clr
  Register #(.width(4)) register_48 (.D(value), .Q(c4), .clk(comparator_48_eq));  // open: en, clr
  Register #(.width(4)) register_49 (.D(value), .Q(c5), .clk(comparator_49_eq));  // open: en, clr
  Register #(.width(4)) register_50 (.D(value), .Q(c6), .clk(comparator_50_eq));  // open: en, clr
  assign controlled_buffer_3_out = com_written ? Clock : 1'bz;  // Controlled_Buffer controlled_buffer_3
  Comparator comparator_51 (.a(card_address), .b(8'hc8), .eq(comparator_51_eq));  // open: gt, lt
  Comparator comparator_52 (.a(card_address), .b(8'hc9), .eq(comparator_52_eq));  // open: gt, lt
  Comparator comparator_53 (.a(card_address), .b(8'hca), .eq(comparator_53_eq));  // open: gt, lt
  Comparator comparator_54 (.a(card_address), .b(8'hcb), .eq(comparator_54_eq));  // open: gt, lt
  Comparator comparator_55 (.a(card_address), .b(8'hcc), .eq(comparator_55_eq));  // open: gt, lt
  Comparator comparator_56 (.a(card_address), .b(8'hcd), .eq(comparator_56_eq));  // open: gt, lt
  Comparator comparator_57 (.a(card_address), .b(8'hce), .eq(comparator_57_eq));  // open: gt, lt
  Comparator comparator_58 (.a(card_address), .b(8'hcf), .eq(comparator_58_eq));  // open: gt, lt
  Comparator comparator_59 (.a(card_address), .b(8'hd0), .eq(comparator_59_eq));  // open: gt, lt
  Comparator comparator_60 (.a(card_address), .b(8'hd1), .eq(comparator_60_eq));  // open: gt, lt
  Comparator comparator_61 (.a(card_address), .b(8'hd2), .eq(comparator_61_eq));  // open: gt, lt
  Comparator comparator_62 (.a(card_address), .b(8'hd3), .eq(comparator_62_eq));  // open: gt, lt
  Comparator comparator_63 (.a(card_address), .b(8'hd4), .eq(comparator_63_eq));  // open: gt, lt
  D_Flip_Flop d_ff_2 (.Q(shocetake), .preset(do_prog), .reset(cdm8_done));  // open: clk, D, Qn, en
  Counter counter_1 (.Q(counter_1_q), .clk(controlled_buffer_3_out), .clr(cdm8_done));  // open: load, D, count, carry
  Register #(.width(4)) register_51 (.D(value), .Q(c8), .clk(comparator_51_eq));  // open: en, clr
  Register #(.width(4)) register_52 (.D(value), .Q(c9), .clk(comparator_52_eq));  // open: en, clr
  Register #(.width(4)) register_53 (.D(value), .Q(ca), .clk(comparator_53_eq));  // open: en, clr
  Register #(.width(4)) register_54 (.D(value), .Q(cb), .clk(comparator_54_eq));  // open: en, clr
  Register #(.width(4)) register_55 (.D(value), .Q(cc), .clk(comparator_55_eq));  // open: en, clr
  Register #(.width(4)) register_56 (.D(value), .Q(cd), .clk(comparator_56_eq));  // open: en, clr
  Register #(.width(4)) register_57 (.D(value), .Q(ce), .clk(comparator_57_eq));  // open: en, clr
  Register #(.width(4)) register_58 (.D(value), .Q(cf), .clk(comparator_58_eq));  // open: en, clr
  Register #(.width(4)) register_59 (.D(value), .Q(d0), .clk(comparator_59_eq));  // open: en, clr
  Register #(.width(4)) register_60 (.D(value), .Q(d1), .clk(comparator_60_eq));  // open: en, clr
  Register #(.width(4)) register_61 (.D(value), .Q(d2), .clk(comparator_61_eq));  // open: en, clr
  Register #(.width(4)) register_62 (.D(value), .Q(d3), .clk(comparator_62_eq));  // open: en, clr
  Register #(.width(4)) register_63 (.D(value), .Q(d4), .clk(comparator_63_eq));  // open: en, clr
  Comparator #(.mode("unsigned")) comparator_64 (.a(counter_1_q), .b({8{1'b1}}), .eq(cdm8_done));  // open: gt, lt
  Register #(.width(4)) register_64 (.D(value), .Q(d6), .clk(comparator_65_eq));  // open: en, clr
  Comparator comparator_65 (.a(card_address), .b(8'hd6), .eq(comparator_65_eq));  // open: gt, lt
  Register #(.width(4)) register_65 (.D(value), .Q(d7), .clk(comparator_66_eq));  // open: en, clr
  Comparator comparator_66 (.a(card_address), .b(8'hd7), .eq(comparator_66_eq));  // open: gt, lt
  Register #(.width(4)) register_66 (.D(value), .Q(d8), .clk(comparator_67_eq));  // open: en, clr
  Comparator comparator_67 (.a(card_address), .b(8'hd8), .eq(comparator_67_eq));  // open: gt, lt
  Register #(.width(4)) register_67 (.D(value), .Q(d9), .clk(comparator_68_eq));  // open: en, clr
  Comparator comparator_68 (.a(card_address), .b(8'hd9), .eq(comparator_68_eq));  // open: gt, lt
  Register #(.width(4)) register_68 (.D(value), .Q(da), .clk(comparator_69_eq));  // open: en, clr
  Comparator comparator_69 (.a(card_address), .b(8'hda), .eq(comparator_69_eq));  // open: gt, lt
  Register #(.width(4)) register_69 (.D(value), .Q(db), .clk(comparator_70_eq));  // open: en, clr
  Comparator comparator_70 (.a(card_address), .b(8'hdb), .eq(comparator_70_eq));  // open: gt, lt
  Register #(.width(4)) register_70 (.D(value), .Q(dc), .clk(comparator_71_eq));  // open: en, clr
  Comparator comparator_71 (.a(card_address), .b(8'hdc), .eq(comparator_71_eq));  // open: gt, lt
  Register #(.width(4)) register_71 (.D(value), .Q(dd), .clk(comparator_72_eq));  // open: en, clr
  Comparator comparator_72 (.a(card_address), .b(8'hdd), .eq(comparator_72_eq));  // open: gt, lt
  Register #(.width(4)) register_72 (.D(value), .Q(de), .clk(comparator_73_eq));  // open: en, clr
  Comparator comparator_73 (.a(card_address), .b(8'hde), .eq(comparator_73_eq));  // open: gt, lt
  Register #(.width(4)) register_73 (.D(value), .Q(df), .clk(comparator_74_eq));  // open: en, clr
  Comparator comparator_74 (.a(card_address), .b(8'hdf), .eq(comparator_74_eq));  // open: gt, lt
  Register #(.width(4)) register_74 (.D(value), .Q(e0), .clk(comparator_75_eq));  // open: en, clr
  Comparator comparator_75 (.a(card_address), .b(8'he0), .eq(comparator_75_eq));  // open: gt, lt
  Register #(.width(4)) register_75 (.D(value), .Q(e1), .clk(comparator_76_eq));  // open: en, clr
  Comparator comparator_76 (.a(card_address), .b(8'he1), .eq(comparator_76_eq));  // open: gt, lt
  Register #(.width(4)) register_76 (.D(value), .Q(e2), .clk(comparator_77_eq));  // open: en, clr
  Comparator comparator_77 (.a(card_address), .b(8'he2), .eq(comparator_77_eq));  // open: gt, lt
  Register #(.width(4)) register_77 (.D(value), .Q(e3), .clk(comparator_78_eq));  // open: en, clr
  Comparator comparator_78 (.a(card_address), .b(8'he3), .eq(comparator_78_eq));  // open: gt, lt
  D_Flip_Flop d_ff_3 (.clk(command_clock), .D(1'b1), .Q(com_written), .reset(cdm8_done));  // open: Qn, preset, en
  or or_3 (or_3_out, _1colod, _2colod, _3colod, _4colod, _5colod, _6colod, _7colod);
  or or_4 (or_4_out, first_usage, cdm8_done);
  and and_5 (do_prog, run_com, com_written, move_done);
  or or_5 (zeroing, reset, cancel_com, run_com);
  Counter counter_2 (.Q(counter_2_q), .clk(d_ff_4_q), .clr(zeroing));  // open: load, D, count, carry
  D_Flip_Flop d_ff_4 (.Q(d_ff_4_q), .preset(or_3_out), .reset(not_6_out));  // open: clk, D, Qn, en
  not not_6 (not_6_out, or_3_out);
  Register register_78 (.D(multiplexer_4_out), .Q(card_address), .clk(command_clock));  // open: en, clr
  Multiplexer #(.width(8), .enable("false")) multiplexer_4 (
    .in0({8{1'b1}}), .in1(command_address), .out(multiplexer_4_out), .sel(to_print));
  Priority_Encoder priority_encoder_1 (
    .in0(1'b0), .in1(_1colod), .in2(_2colod), .in3(_3colod), .in4(_4colod), .in5(_5colod), .in6(_6colod),
    .in7(_7colod), .out(priority_encoder_1_out), .gs(new_com));  // open: en_in, en_out
  Multiplexer #(.width(8), .enable("false")) multiplexer_5 (
    .in0(current_command), .in1({8{1'b0}}), .out(multiplexer_5_out), .sel(zeroing));
  and and_6 (to_print, or_4_out, sent_done);
  Comparator #(.mode("unsigned")) comparator_79 (.a(counter_2_q), .b({8{1'b0}}), .eq(first_usage));  // open: gt, lt
  Pull_Resistor pull_resistor_2 (.node(priority_encoder_1_out));
  Register register_79 (.D(multiplexer_5_out), .Q(register_79_q), .clk(Clock));  // open: en, clr
  card_replace card_replace_1 (
    .colod_number(priority_encoder_1_out), .cur_command(register_79_q), .updated_program(current_command),
    .move_done_updated(move_done));
  assign command_address = to_print ? print_cards_1_adr : 8'bz;  // Controlled_Buffer controlled_buffer_4
  assign command_clock = to_print ? pull_resistor_3_node : 1'bz;  // Controlled_Buffer controlled_buffer_5
  Pull_Resistor pull_resistor_3 (.node(pull_resistor_3_node));
  assign pull_resistor_3_node = to_print ? Clock : 1'bz;  // Controlled_Buffer controlled_buffer_6
  and and_7 (and_7_out, gen_done, sent_done, ~to_print);  // AND_Gate
  and and_8 (and_8_out, gen_done, sent_done, ~to_print);  // AND_Gate
  Hex_Digit_Display hex_digit_display_1 (.value(current_command[7:4]));  // open: dp
  assign print_ld = to_print ? print_cards_1_print : 1'bz;  // Controlled_Buffer controlled_buffer_7
  print_cards print_cards_1 (
    .clock(pull_resistor_3_node), .adr(print_cards_1_adr), .print(print_cards_1_print), .move_done(or_6_out));
  or or_6 (or_6_out, move_done, reset);
  assign command_data = and_7_out ? current_command : 8'bz;  // Controlled_Buffer controlled_buffer_8
  assign command_clock = and_8_out ? Clock : 1'bz;  // Controlled_Buffer controlled_buffer_9
  Button button_2 (.out(reset));
  Button button_3 (.out(run_com));
  Button button_4 (.out(cancel_com));
  Hex_Digit_Display hex_digit_display_2 (.value(current_command[3:0]));  // open: dp
  not not_7 (not_7_out, not_7_out);
  write_sentinels write_sentinels_1 (
    .data(gen_data), .clock(Clock), .reset(gen_done), .address(command_address), .sent_done(sent_done),
    .sent_ld(gen_ld));
  Button button_5 (.out(_1colod));
  Hex_Digit_Display hex_digit_display_3 (.value(_91));  // open: dp
  Hex_Digit_Display hex_digit_display_4 (.value(_92));  // open: dp
  Hex_Digit_Display hex_digit_display_5 (.value(_93));  // open: dp
  Hex_Digit_Display hex_digit_display_6 (.value(_94));  // open: dp
  Hex_Digit_Display hex_digit_display_7 (.value(_95));  // open: dp
  Hex_Digit_Display hex_digit_display_8 (.value(_96));  // open: dp
  Hex_Digit_Display hex_digit_display_9 (.value(_97));  // open: dp
  Hex_Digit_Display hex_digit_display_10 (.value(_98));  // open: dp
  generator generator_1 (
    .clock(Clock), .reset(reset), .data(gen_data), .address(command_address), .gen_done(gen_done),
    .gen_ld(gen_ld));
  and and_9 (and_9_out, gen_done, sent_done, ~to_print);  // AND_Gate
  assign command_ld = and_9_out ? 1'b1 : 1'bz;  // Controlled_Buffer controlled_buffer_10
  and and_10 (and_10_out, gen_done, sent_done, ~to_print);  // AND_Gate
  assign command_address = and_10_out ? 8'hf3 : 8'bz;  // Controlled_Buffer controlled_buffer_11
  Button button_6 (.out(_2colod));
  Hex_Digit_Display hex_digit_display_11 (.value(_9a));  // open: dp
  Hex_Digit_Display hex_digit_display_12 (.value(_9b));  // open: dp
  Hex_Digit_Display hex_digit_display_13 (.value(_9c));  // open: dp
  Hex_Digit_Display hex_digit_display_14 (.value(_9d));  // open: dp
  Hex_Digit_Display hex_digit_display_15 (.value(_9e));  // open: dp
  Hex_Digit_Display hex_digit_display_16 (.value(_9f));  // open: dp
  Hex_Digit_Display hex_digit_display_17 (.value(a0));  // open: dp
  Hex_Digit_Display hex_digit_display_18 (.value(a1));  // open: dp
  Hex_Digit_Display hex_digit_display_19 (.value(a2));  // open: dp
  Button button_7 (.out(_3colod));
  Hex_Digit_Display hex_digit_display_20 (.value(a4));  // open: dp
  Hex_Digit_Display hex_digit_display_21 (.value(a5));  // open: dp
  Hex_Digit_Display hex_digit_display_22 (.value(a6));  // open: dp
  Hex_Digit_Display hex_digit_display_23 (.value(a7));  // open: dp
  Hex_Digit_Display hex_digit_display_24 (.value(a8));  // open: dp
  Hex_Digit_Display hex_digit_display_25 (.value(a9));  // open: dp
  Hex_Digit_Display hex_digit_display_26 (.value(aa));  // open: dp
  Hex_Digit_Display hex_digit_display_27 (.value(ab));  // open: dp
  Hex_Digit_Display hex_digit_display_28 (.value(ac));  // open: dp
  Hex_Digit_Display hex_digit_display_29 (.value(ad));  // open: dp
  Button button_8 (.out(_4colod));
  Hex_Digit_Display hex_digit_display_30 (.value(af));  // open: dp
  Hex_Digit_Display hex_digit_display_31 (.value(b0));  // open: dp
  Hex_Digit_Display hex_digit_display_32 (.value(b1));  // open: dp
  Hex_Digit_Display hex_digit_display_33 (.value(b2));  // open: dp
  Hex_Digit_Display hex_digit_display_34 (.value(b3));  // open: dp
  Hex_Digit_Display hex_digit_display_35 (.value(b4));  // open: dp
  Hex_Digit_Display hex_digit_display_36 (.value(b5));  // open: dp
  Hex_Digit_Display hex_digit_display_37 (.value(b6));  // open: dp
  Hex_Digit_Display hex_digit_display_38 (.value(b7));  // open: dp
  Hex_Digit_Display hex_digit_display_39 (.value(b8));  // open: dp
  Hex_Digit_Display hex_digit_display_40 (.value(b9));  // open: dp
  Button button_9 (.out(_5colod));
  Hex_Digit_Display hex_digit_display_41 (.value(bb));  // open: dp
  Hex_Digit_Display hex_digit_display_42 (.value(bc));  // open: dp
  Hex_Digit_Display hex_digit_display_43 (.value(bd));  // open: dp
  Hex_Digit_Display hex_digit_display_44 (.value(be));  // open: dp
  Hex_Digit_Display hex_digit_display_45 (.value(bf));  // open: dp
  Hex_Digit_Display hex_digit_display_46 (.value(c0));  // open: dp
  Hex_Digit_Display hex_digit_display_47 (.value(c1));  // open: dp
  Hex_Digit_Display hex_digit_display_48 (.value(c2));  // open: dp
  Hex_Digit_Display hex_digit_display_49 (.value(c3));  // open: dp
  Hex_Digit_Display hex_digit_display_50 (.value(c4));  // open: dp
  Hex_Digit_Display hex_digit_display_51 (.value(c5));  // open: dp
  Hex_Digit_Display hex_digit_display_52 (.value(c6));  // open: dp
  Button button_10 (.out(_6colod));
  Hex_Digit_Display hex_digit_display_53 (.value(c8));  // open: dp
  Hex_Digit_Display hex_digit_display_54 (.value(c9));  // open: dp
  Hex_Digit_Display hex_digit_display_55 (.value(ca));  // open: dp
  Hex_Digit_Display hex_digit_display_56 (.value(cb));  // open: dp
  Hex_Digit_Display hex_digit_display_57 (.value(cc));  // open: dp
  Hex_Digit_Display hex_digit_display_58 (.value(cd));  // open: dp
  Hex_Digit_Display hex_digit_display_59 (.value(ce));  // open: dp
  Hex_Digit_Display hex_digit_display_60 (.value(cf));  // open: dp
  Hex_Digit_Display hex_digit_display_61 (.value(d0));  // open: dp
  Hex_Digit_Display hex_digit_display_62 (.value(d1));  // open: dp
  Hex_Digit_Display hex_digit_display_63 (.value(d2));  // open: dp
  Hex_Digit_Display hex_digit_display_64 (.value(d3));  // open: dp
  Hex_Digit_Display hex_digit_display_65 (.value(d4));  // open: dp
  Button button_11 (.out(_7colod));
  Hex_Digit_Display hex_digit_display_66 (.value(d6));  // open: dp
  Hex_Digit_Display hex_digit_display_67 (.value(d7));  // open: dp
  Hex_Digit_Display hex_digit_display_68 (.value(d8));  // open: dp
  Hex_Digit_Display hex_digit_display_69 (.value(d9));  // open: dp
  Hex_Digit_Display hex_digit_display_70 (.value(da));  // open: dp
  Hex_Digit_Display hex_digit_display_71 (.value(db));  // open: dp
  Hex_Digit_Display hex_digit_display_72 (.value(dc));  // open: dp
  Hex_Digit_Display hex_digit_display_73 (.value(dd));  // open: dp
  Hex_Digit_Display hex_digit_display_74 (.value(de));  // open: dp
  Hex_Digit_Display hex_digit_display_75 (.value(df));  // open: dp
  Hex_Digit_Display hex_digit_display_76 (.value(e0));  // open: dp
  Hex_Digit_Display hex_digit_display_77 (.value(e1));  // open: dp
  Hex_Digit_Display hex_digit_display_78 (.value(e2));  // open: dp
  Hex_Digit_Display hex_digit_display_79 (.value(e3));  // open: dp

  // Other names for the same wires on the sheet: RAM_data[7:0] = card_value; print_clock = command_clock;
  //   ram_clock = command_clock; gen_address[7:0] = command_address; IO_address[7:0] = command_address;
  //   print_address[7:0] = command_address; ram_address_t[7:0] = command_address; sent_address[7:0] = command_address;
  //   IO_data[7:0] = gen_data; sent_data[7:0] = gen_data; IO_out_in_prime = gen_ld; IO_sel = gen_ld; sent_ld = gen_ld

  // Notes on the sheet:
  //   Value reading
  //   Card printer
  //   Updating indicators
  //   contents of rom_1 (hex, n*v repeats v):
  //   d5 ee 0 d0 ff c1 d1 b a4 c5 cd 0 d9 d2 f3 ba d0 f 42 d6 59 d0 40 bd 41 e0 1e 8f ee 17 c3 8b bd d2 f3
  //   ba 4*9a d6 59 d0 f 41 89 89 e1 33 ee 3 8d be 42 e1 3a ee 3 76 e0 40 8f ee 34 d0 7f 8b be 42 ae 8f c5
  //   d0 40 be 42 e0 57 be a6 d2 0 ae 8f 8d ee 4a ee 3 d3 80 8a 1b bf d0 80 8f be 42 e0 67 ee 60 d7 24*0
  //   90 99 a3 ae ba c7 d5 105*0 d
  //   Addresses to RAM
  //   Data to/from RAM
  //   Card replacer
  //   Read/print to RAM
  //   RAM clock
  //   Print cards to indicators
  //   from
  //   Reset game
  //   Run command
  //   Cancel command
  //   Current command
  //   to
  //   C - closed card
  //   0 - empty cell
  //   Add sentinels
  //   Write command to RAM
  //   Writes right after main colod generated
  //   Generate colod
endmodule

module configuration (
  input  [31:0] colods,
  input  clock,
  input  enable,
  output [31:0] final_colod,
  output [3:0] card
);

  wire new_taken_prime;
  wire [2:0] adder_1_out;
  wire [3:3] adder_1_cout;
  wire [4:0] new_card;
  wire [31:0] controlled_buffer_1_out, shifter_1_out;

  // Probe on new_card
  Random #(.width(5)) random_1 (.clk(clock), .next(enable), .out(new_card));  // open: clr
  Multiplexer #(.select(5), .enable("false")) multiplexer_1 (
    .in0(colods[0]), .in1(colods[1]), .in2(colods[2]), .in3(colods[3]), .in4(colods[4]), .in5(colods[5]),
    .in6(colods[6]), .in7(colods[7]), .in8(colods[8]), .in9(colods[9]), .in10(colods[10]), .in11(colods[11]),
    .in12(colods[12]), .in13(colods[13]), .in14(colods[14]), .in15(colods[15]), .in16(colods[16]),
    .in17(colods[17]), .in18(colods[18]), .in19(colods[19]), .in20(colods[20]), .in21(colods[21]),
    .in22(colods[22]), .in23(colods[23]), .in24(colods[24]), .in25(colods[25]), .in26(colods[26]),
    .in27(colods[27]), .in28(colods[28]), .in29(colods[29]), .in30(colods[30]), .in31(colods[31]),
    .out(new_taken_prime), .sel(new_card));
  Shifter #(.width(32)) shifter_1 (.in(32'h1), .\dist (new_card), .out(shifter_1_out));
  assign controlled_buffer_1_out = enable ? shifter_1_out : 32'bz;  // Controlled_Buffer controlled_buffer_1
  Pull_Resistor pull_resistor_1 (.node(controlled_buffer_1_out));
  assign final_colod = ~controlled_buffer_1_out & colods;  // AND_Gate and_1, 32 bits wide
  Adder #(.width(3)) adder_1 (.a(new_card[2:0]), .b(3'b010), .out(adder_1_out), .cout(adder_1_cout[3]));  // open: cin
  Pull_Resistor pull_resistor_2 (.node(card));
  assign card = new_taken_prime ? {adder_1_cout[3], adder_1_out} : 4'bz;  // Controlled_Buffer controlled_buffer_2
endmodule

module generator (
  input  clock,
  input  reset,
  output [7:0] address,
  output [7:0] data,
  output gen_done,
  output gen_ld
);

  wire card_gen, comparator_1_eq, comparator_2_eq, comparator_3_eq, comparator_4_eq, comparator_5_eq,
       comparator_6_eq, comparator_7_eq, comparator_8_eq, gen_clock, gen_done_t, gen_in_prog,
       gen_in_prog_prime, next_card, not_3_out, or_1_out;
  wire [3:0] configuration_1_card;
  wire [4:0] counter_1_q;
  wire [7:0] addr;
  wire [7:7] not_1_out;
  wire [31:0] configuration_1_final_colod, multiplexer_2_out, register_1_q;

  S_R_Flip_Flop s_r_ff_1 (
    .S(reset), .clk(clock), .R(gen_done_t), .Q(gen_in_prog), .Qn(gen_in_prog_prime));  // open: preset, reset, en
  Multiplexer #(.select(5), .width(8), .disabled(0), .enable("false")) multiplexer_1 (
    .in0(8'h91), .in1(8'h92), .in2(8'h9a), .in3(8'h9b), .in4(8'h9c), .in5(8'ha4), .in6(8'ha5), .in7(8'ha6),
    .in8(8'ha7), .in9(8'haf), .in10(8'hb0), .in11(8'hb1), .in12(8'hb2), .in13(8'hb3), .in14(8'hbb),
    .in15(8'hbc), .in16(8'hbd), .in17(8'hbe), .in18(8'hbf), .in19(8'hc8), .in20(8'hc9), .in21(8'hca),
    .in22(8'hcb), .in23(8'hcc), .in24(8'hcd), .in25(8'hd6), .in26(8'hd7), .in27(8'hd8), .in28(8'hd9),
    .in29(8'hda), .in30(8'hdb), .in31(8'hdc), .out(addr), .sel(counter_1_q));
  and and_1 (gen_clock, clock, gen_in_prog);
  and and_2 (next_card, gen_clock, card_gen);
  Counter #(.width(5), .max('h1f)) counter_1 (
    .count(gen_in_prog), .Q(counter_1_q), .clk(next_card), .clr(reset));  // open: load, D, carry
  Comparator comparator_1 (.a(8'h92), .b(addr), .eq(comparator_1_eq));  // open: gt, lt
  Comparator comparator_2 (.a(8'h9c), .b(addr), .eq(comparator_2_eq));  // open: gt, lt
  Comparator comparator_3 (.a(8'ha7), .b(addr), .eq(comparator_3_eq));  // open: gt, lt
  Comparator comparator_4 (.a(8'hb3), .b(addr), .eq(comparator_4_eq));  // open: gt, lt
  Comparator comparator_5 (.a(8'hbf), .b(addr), .eq(comparator_5_eq));  // open: gt, lt
  Comparator comparator_6 (.a(8'hcd), .b(addr), .eq(comparator_6_eq));  // open: gt, lt
  Comparator comparator_7 (.a(8'hdc), .b(addr), .eq(comparator_7_eq));  // open: gt, lt
  or or_1 (or_1_out, comparator_1_eq, comparator_2_eq, comparator_3_eq, comparator_4_eq, comparator_5_eq, comparator_6_eq, comparator_7_eq);
  assign address = next_card ? addr : 8'bz;  // Controlled_Buffer controlled_buffer_1
  Register #(.width(32)) register_1 (.D(multiplexer_2_out), .Q(register_1_q), .clk(clock));  // open: en, clr
  Multiplexer #(.width(32), .enable("false")) multiplexer_2 (
    .in0({32{1'b1}}), .in1(configuration_1_final_colod), .out(multiplexer_2_out), .sel(gen_in_prog));
  not not_1 (not_1_out[7], or_1_out);
  // Probe on configuration_1_final_colod
  assign data = next_card ? {not_1_out[7], 3'b100, configuration_1_card} : 8'bz;  // Controlled_Buffer controlled_buffer_2
  configuration configuration_1 (
    .clock(gen_clock), .card(configuration_1_card), .enable(gen_in_prog), .colods(register_1_q),
    .final_colod(configuration_1_final_colod));
  Hex_Digit_Display hex_digit_display_1 (.value(configuration_1_card));  // open: dp
  not not_2 (card_gen, comparator_8_eq);
  Comparator #(.width(4)) comparator_8 (.a(4'b0000), .b(configuration_1_card), .eq(comparator_8_eq));  // open: gt, lt
  Comparator #(.width(32)) comparator_9 (
    .a({32{1'b0}}), .b(configuration_1_final_colod), .eq(gen_done_t));  // open: gt, lt
  and and_3 (gen_done, gen_in_prog_prime, not_3_out);
  not not_3 (not_3_out, gen_in_prog_prime);
  assign gen_ld = gen_in_prog ? next_card : 1'bz;  // Controlled_Buffer controlled_buffer_3

  // Other names for the same wires on the sheet: print_card = next_card

  // Notes on the sheet:
  //   1 colon
  //   2 colon
  //   3 colon
  //   4 colon
  //   5 colon
  //   6 colon
  //   7 colon
  //   opened
  //   sentinels
  //   Rising edge
  //   Chooses random card from colod
endmodule

module write_sentinels (
  input  clock,
  input  reset,
  output [7:0] address,
  output [7:0] data,
  output sent_done,
  output sent_ld
);

  wire not_1_out, sen_done, sen_in_prog, sen_in_prog_prime, write_sent;
  wire [2:0] counter_1_q;
  wire [7:0] addr;

  S_R_Flip_Flop s_r_ff_1 (
    .S(reset), .clk(clock), .R(sen_done), .Q(sen_in_prog), .Qn(sen_in_prog_prime));  // open: preset, reset, en
  Multiplexer #(.select(3), .width(8), .disabled(0), .enable("false")) multiplexer_1 (
    .in0(8'h90), .in1(8'h99), .in2(8'ha3), .in3(8'hae), .in4(8'hba), .in5(8'hc7), .in6(8'hd5), .out(addr),
    .sel(counter_1_q));  // open: in7
  Counter #(.width(3), .max('h7)) counter_1 (
    .count(sen_in_prog), .Q(counter_1_q), .clk(clock), .clr(reset));  // open: load, D, carry
  and and_1 (write_sent, clock, sen_in_prog);
  assign address = write_sent ? addr : 8'bz;  // Controlled_Buffer controlled_buffer_1
  Comparator #(.width(3), .mode("unsigned")) comparator_1 (.a(3'b111), .b(counter_1_q), .eq(sen_done));  // open: gt, lt
  assign data = write_sent ? 8'ha : 8'bz;  // Controlled_Buffer controlled_buffer_2
  not not_1 (not_1_out, sen_in_prog_prime);
  assign sent_ld = sen_in_prog ? write_sent : 1'bz;  // Controlled_Buffer controlled_buffer_3
  and and_2 (sent_done, sen_in_prog_prime, not_1_out);

  // Notes on the sheet:
  //   opened
  //   sentinels
endmodule

module card_replace (
  input  [2:0] colod_number,
  input  [7:0] cur_command,
  output [7:0] updated_program,
  output move_done_updated
);

  wire _1st_done, _2st_done, and_1_out, and_2_out, and_3_out, and_4_out, and_5_out, and_6_out, and_7_out,
       and_8_out, colod_isnt_0, comparator_1_eq, not_equal, or_3_out, or_4_out;

  Comparator #(.width(3), .mode("unsigned")) comparator_1 (
    .a(colod_number), .b(3'b000), .eq(comparator_1_eq));  // open: gt, lt
  not not_1 (colod_isnt_0, comparator_1_eq);
  Comparator #(.width(3), .mode("unsigned")) comparator_2 (
    .a(colod_number), .b(cur_command[2:0]), .eq(not_equal));  // open: gt, lt
  or or_1 (_1st_done, cur_command[0], cur_command[1], cur_command[2], cur_command[3]);
  or or_2 (_2st_done, cur_command[4], cur_command[5], cur_command[6], cur_command[7]);
  and and_1 (and_1_out, _1st_done, _2st_done);
  or or_3 (or_3_out, updated_program[0], updated_program[1], updated_program[2], updated_program[3]);
  and and_2 (and_2_out, or_3_out, or_4_out);
  or or_4 (or_4_out, updated_program[4], updated_program[5], updated_program[6], updated_program[7]);
  or or_5 (move_done_updated, and_1_out, and_2_out);
  and and_3 (and_3_out, _1st_done, colod_isnt_0, _2st_done, ~not_equal);  // AND_Gate
  and and_4 (and_4_out, _1st_done, ~colod_isnt_0, _2st_done, ~not_equal);  // AND_Gate
  and and_5 (and_5_out, _1st_done, colod_isnt_0, ~_2st_done, ~not_equal);  // AND_Gate
  and and_6 (and_6_out, ~_1st_done, colod_isnt_0, ~_2st_done, ~not_equal);  // AND_Gate
  and and_7 (and_7_out, _1st_done, ~colod_isnt_0, ~_2st_done, ~not_equal);  // AND_Gate
  and and_8 (and_8_out, ~_1st_done, ~colod_isnt_0, ~_2st_done, ~not_equal);  // AND_Gate
  assign updated_program = and_3_out ? cur_command : 8'bz;  // Controlled_Buffer controlled_buffer_1
  assign updated_program = and_4_out ? cur_command : 8'bz;  // Controlled_Buffer controlled_buffer_2
  assign updated_program = and_5_out ? {1'b0, colod_number, cur_command[3:0]} : 8'bz;  // Controlled_Buffer controlled_buffer_3
  assign updated_program = and_6_out ? {cur_command[7:4], 1'b0, colod_number} : 8'bz;  // Controlled_Buffer controlled_buffer_4
  assign updated_program = and_7_out ? cur_command : 8'bz;  // Controlled_Buffer controlled_buffer_5
  assign updated_program = and_8_out ? cur_command : 8'bz;  // Controlled_Buffer controlled_buffer_6
  assign updated_program = not_equal ? cur_command : 8'bz;  // Controlled_Buffer controlled_buffer_7

  // Other names for the same wires on the sheet: c[2:0] = colod_number;
  //   case1 (some bits) = {cur_command[7:4], colod_number}; case2[6:0] = {colod_number, cur_command[3:0]};
  //   case3[7:0] = cur_command; command[7:0] = cur_command; res[7:0] = updated_program
endmodule

module print_cards (
  input  clock,
  input  move_done,
  output [7:0] adr,
  output print
);

  wire pull_resistor_1_node;
  wire [7:0] adr_t;

  Counter counter_1 (.Q(adr_t), .clk(pull_resistor_1_node), .clr(move_done));  // open: load, D, count, carry
  Pull_Resistor pull_resistor_1 (.node(pull_resistor_1_node));
  assign pull_resistor_1_node = print ? clock : 1'bz;  // Controlled_Buffer controlled_buffer_1
  Comparator comparator_1 (.a(adr_t), .b(8'h4d), .lt(print));  // open: gt, eq
  ROM rom_1 (.addr(adr_t), .data(adr));  // open: sel

  // Notes on the sheet:
  //   sentinels
  //   cards
  //   contents of rom_1 (hex, n*v repeats v):
  //   91 92 93 94 95 96 97 98 9a 9b 9c 9d 9e 9f a0 a1 a2 a4 a5 a6 a7 a8 a9 aa ab ac ad af b0 b1 b2 b3 b4
  //   b5 b6 b7 b8 b9 bb bc bd be bf c0 c1 c2 c3 c4 c5 c6 c8 c9 ca cb cc cd ce cf d0 d1 d2 d3 d4 d6 d7 d8
  //   d9 da db dc dd de df e0 e1 e2 e3 e4
endmodule
